// Logisim project cpu24.circ as structural Verilog: 16 circuits, main circuit ◇单周期MIPS
module \单周期MIPS  (
  output RegWrite,
  output MemWrite,
  output [31:0] PC,
  output [31:0] IR,
  output [31:0] RDin,
  output [31:0] MDin
);

  wire and_1_out, and_2_out, and_3_out, CLK, comparator_1_eq, Go, IR1, IR2, IR3, mips_alu_1_equal, not_1_out,
       or_1_out, or_2_out, Running, SignedExt, Syscall, W1, W2, W3, \单周期硬布线控制器_1_p1 , \单周期硬布线控制器_1_p2 ,
       \单周期硬布线控制器_1_p7 , \单周期硬布线控制器_1_p8 , \单周期硬布线控制器_1_p9 , \单周期硬布线控制器_1_p12 , \单周期硬布线控制器_1_p14 ,
       \单周期硬布线控制器_1_p15 ;
  wire [3:0] \单周期硬布线控制器_1_p11 ;
  wire [4:0] multiplexer_4_out, multiplexer_5_out, multiplexer_6_out, multiplexer_7_out;
  wire [15:0] \总周期数 ;
  wire [31:0] adder_1_out, adder_2_out, bit_extender_1_out, bit_extender_2_out, LedData, mips_alu_1_result,
       multiplexer_1_out, multiplexer_2_out, multiplexer_3_out, multiplexer_9_out, multiplexer_10_out,
       multiplexer_11_out, R1, ram_1_data, shifter_1_out;

  Clock #(.highDuration(1), .lowDuration(1)) clock_1 (.out(CLK));
  Button _1 (.out(IR1));
  Button _2 (.out(IR2));
  Button _3 (.out(IR3));
  Button \u_继续运行  (.out(Go));
  LED #(.active("true")) led_1 (.in(W1));
  LED #(.active("true")) led_2 (.in(W2));
  LED #(.active("true")) led_3 (.in(W3));
  Hex_Digit_Display hex_digit_display_1 (.value(LedData[31:28]));  // open: dp
  Hex_Digit_Display hex_digit_display_2 (.value(LedData[23:20]));  // open: dp
  Hex_Digit_Display hex_digit_display_3 (.value(LedData[27:24]));  // open: dp
  Multiplexer #(.select(1), .width(32), .disabled("Z"), .enable("false")) multiplexer_1 (
    .in0(adder_1_out), .in1({adder_1_out[31:28], IR[25:0], 2'b00}), .out(multiplexer_1_out), .sel(or_1_out));
  Multiplexer #(.select(1), .width(32), .disabled("Z"), .enable("false")) multiplexer_2 (
    .in0(multiplexer_1_out), .in1(R1), .out(multiplexer_2_out), .sel(\单周期硬布线控制器_1_p2 ));
  Hex_Digit_Display hex_digit_display_4 (.value(LedData[15:12]));  // open: dp
  Hex_Digit_Display hex_digit_display_5 (.value(LedData[19:16]));  // open: dp
  // Probe on multiplexer_3_out
  Multiplexer #(.select(1), .width(32), .disabled("Z"), .enable("false")) multiplexer_3 (
    .in0(multiplexer_2_out), .in1(adder_2_out), .out(multiplexer_3_out), .sel(or_2_out));
  Register #(.width(32), .trigger("rising"), .Select("low")) u_PC (
    .D(multiplexer_3_out), .en(Running), .Q(PC), .clk(CLK), .clr(Go));
  Hex_Digit_Display hex_digit_display_6 (.value(LedData[7:4]));  // open: dp
  Hex_Digit_Display hex_digit_display_7 (.value(LedData[11:8]));  // open: dp
  // Probe on \总周期数 
  Hex_Digit_Display hex_digit_display_8 (.value(LedData[3:0]));  // open: dp
  or or_1 (or_1_out, \单周期硬布线控制器_1_p14 , \单周期硬布线控制器_1_p1 );
  Adder #(.width(32)) adder_1 (.a(PC), .b(32'h4), .out(adder_1_out));  // open: cin, cout
  // Probe on IR[31:26]
  // Probe on IR[25:21]
  ROM #(.addrWidth(10), .dataWidth(32), .Select("high")) rom_1 (.addr(PC[11:2]), .data(IR));
  // Probe on IR[20:16]
  // Probe on IR[15:11]
  // 单周期硬布线控制器 单周期硬布线控制器_1: pin names not known; wires that end beside it: \单周期硬布线控制器_1_p1 , \单周期硬布线控制器_1_p2 , SignedExt, IR[31:26], IR[5:0], Syscall, \单周期硬布线控制器_1_p7 , \单周期硬布线控制器_1_p8 , \单周期硬布线控制器_1_p9 , MemWrite, \单周期硬布线控制器_1_p11 , \单周期硬布线控制器_1_p12 , RegWrite, \单周期硬布线控制器_1_p14 , \单周期硬布线控制器_1_p15 
  // Probe on IR[5:0]
  Multiplexer #(.select(1), .width(5), .disabled("Z"), .enable("false")) multiplexer_4 (
    .in0(IR[25:21]), .in1(5'b00010), .out(multiplexer_4_out), .sel(Syscall));
  Multiplexer #(.select(1), .width(5), .disabled("Z"), .enable("false")) multiplexer_5 (
    .in0(IR[20:16]), .in1(5'b00100), .out(multiplexer_5_out), .sel(Syscall));
  Multiplexer #(.select(1), .width(5), .disabled("Z"), .enable("false")) multiplexer_6 (
    .in0(IR[20:16]), .in1(IR[15:11]), .out(multiplexer_6_out), .sel(\单周期硬布线控制器_1_p15 ));
  Multiplexer #(.select(1), .width(5), .disabled("Z"), .enable("false")) multiplexer_7 (
    .in0(multiplexer_6_out), .in1({5{1'b1}}), .out(multiplexer_7_out), .sel(\单周期硬布线控制器_1_p14 ));
  Multiplexer #(.select(1), .width(32), .disabled("Z"), .enable("false")) multiplexer_8 (
    .in0(multiplexer_11_out), .in1(adder_1_out), .out(RDin), .sel(\单周期硬布线控制器_1_p14 ));
  assign bit_extender_1_out = {{16{1'b0}}, IR[15:0]};  // Bit_Extender bit_extender_1
  assign bit_extender_2_out = {{16{IR[15]}}, IR[15:0]};  // Bit_Extender bit_extender_2
  or or_2 (or_2_out, and_2_out, and_1_out);
  MIPS_Regifile mips_regifile_1 (
    .Din(RDin), .Clk(CLK), .R1(R1), .R2(MDin), .WE(RegWrite), .W_num(multiplexer_7_out),
    .R1_num(multiplexer_4_out), .R2_num(multiplexer_5_out));
  Multiplexer #(.select(1), .width(32), .disabled("Z"), .enable("false")) multiplexer_9 (
    .in0(bit_extender_1_out), .in1(bit_extender_2_out), .out(multiplexer_9_out), .sel(SignedExt));
  Multiplexer #(.select(1), .width(32), .disabled("Z"), .enable("false")) multiplexer_10 (
    .in0(MDin), .in1(multiplexer_9_out), .out(multiplexer_10_out), .sel(\单周期硬布线控制器_1_p12 ));
  Shifter #(.width(32), .shift("ll")) shifter_1 (.in(bit_extender_2_out), .\dist (5'b00010), .out(shifter_1_out));
  and and_1 (and_1_out, \单周期硬布线控制器_1_p7 , mips_alu_1_equal);
  // Probe on R1
  // Probe on multiplexer_10_out
  Adder #(.width(32)) adder_2 (.a(shifter_1_out), .b(adder_1_out), .out(adder_2_out));  // open: cin, cout
  and and_2 (and_2_out, \单周期硬布线控制器_1_p8 , ~mips_alu_1_equal);  // AND_Gate
  MIPS_ALU mips_alu_1 (
    .X(R1), .Y(multiplexer_10_out), .AluOP(\单周期硬布线控制器_1_p11 ), .Equal(mips_alu_1_equal),
    .Result(mips_alu_1_result), .shamt(IR[10:6]));  // open: Result_2
  // Probe on IR[10:6]
  RAM #(.addrWidth(10), .dataWidth(32), .bus("separate"), .Select("high")) ram_1 (
    .addr(mips_alu_1_result[11:2]), .din(MDin), .data(ram_1_data), .str(MemWrite), .sel(Running), .clk(CLK),
    .clr(Go));  // open: ld
  Multiplexer #(.select(1), .width(32), .disabled("Z"), .enable("false")) multiplexer_11 (
    .in0(mips_alu_1_result), .in1(ram_1_data), .out(multiplexer_11_out), .sel(\单周期硬布线控制器_1_p9 ));
  Button \u_总复位  (.out(Go));
  Comparator #(.width(32), .mode("twosComplement")) comparator_1 (
    .a(32'h22), .b(R1), .eq(comparator_1_eq));  // open: gt, lt
  and and_3 (and_3_out, comparator_1_eq, Syscall);
  not not_1 (not_1_out, comparator_1_eq);
  Register #(.width(32), .trigger("rising"), .Select("low")) register_1 (
    .D(MDin), .en(and_3_out), .Q(LedData), .clk(CLK), .clr(Go));
  D_Flip_Flop #(.trigger("rising"), .Pre_Clr_Positions("ABOVE_BELOW"), .NegatePresetClear("false"), .enable("true"), .NewFFLayout("true")) d_ff_1 (
    .clk(CLK), .D(not_1_out), .Qn(Running), .en(Syscall), .reset(Go));  // open: Q, preset
  Counter #(.width(16), .max('hffff), .ongoal("wrap"), .trigger("rising"), .behavior("old")) \u_总周期数  (
    .count(Running), .Q(\总周期数 ), .carry(Go), .clk(CLK));  // open: load, D, clr, preset

  // Other names for the same wires on the sheet: R2[31:0] = MDin; RST = Go

  // Notes on the sheet:
  //   中断源
  //   中断等待指示
  //   总复位信号应将除ROM以外所有存储组件全部清零
  //   数码管输出
  //   数码管输出应该用寄存器锁存，否则显示数据只能一闪而过
  //   指令存储器
  //   OP
  //   Func
  //   rs
  //   指令字
  //   contents of rom_1 (hex, n*v repeats v):
  //   20110100 20020022 8000006 20110004 20120005 20130006 10000003 20110007 20120008 20130009 14110003
  //   2011000a 2012000b 2013000c c000014 2002000a 0 0 0 c 2231ffff 0 0 0 112020 0 0 0 c 1620fff6 3e00008
  //   rt
  //   rd
  //   JMP
  //   JR
  //   OP
  //   Func
  //   Syscall
  //   Bne
  //   MemToReg
  //   MemWrite
  //   AluOP
  //   AluSrcB
  //   RegWrite
  //   JAL
  //   RegDst
  //   为方便自动评测，需要输出PC，IR，寄存器文件写入端口RDin，内存写入端口MDin等信号
endmodule

// 单周期硬布线控制器
module \单周期硬布线控制器  (
  input  [5:0] OP,
  input  [5:0] Func,
  output [3:0] ALU_OP,
  output MemToReg,
  output MemWrite,
  output ALU_SRC,
  output RegWrite,
  output SysCALL,
  output SignedExt,
  output RegDst,
  output Beq,
  output Bne,
  output JR,
  output JMP,
  output JAL,
  output RS_SHAMT,
  output SB,
  output BLTZ,
  output R1_Used,
  output R2_Used
);

  \运算控制器自动生成  \u_运算控制器自动生成_1  (
    .OP0(OP[0]), .OP1(OP[1]), .OP2(OP[2]), .OP3(OP[3]), .OP4(OP[4]), .OP5(OP[5]), .F0(Func[0]), .F1(Func[1]),
    .F2(Func[2]), .F3(Func[3]), .F4(Func[4]), .F5(Func[5]), .S0(ALU_OP[0]), .S1(ALU_OP[1]), .S2(ALU_OP[2]),
    .S3(ALU_OP[3]));
  \控制信号自动生成  \u_控制信号自动生成_1  (
    .OP0(OP[0]), .OP1(OP[1]), .OP2(OP[2]), .OP3(OP[3]), .OP4(OP[4]), .OP5(OP[5]), .F0(Func[0]), .F1(Func[1]),
    .F2(Func[2]), .F3(Func[3]), .F4(Func[4]), .F5(Func[5]), .MemToReg(MemToReg), .MemWrite(MemWrite),
    .ALU_SRC(ALU_SRC), .RegWrite(RegWrite), .SysCALL(SysCALL), .SignedExt(SignedExt), .RegDst(RegDst),
    .BEQ(Beq), .BNE(Bne), .JR(JR), .JUMP(JMP), .JAL(JAL), .RS_SHAMT(RS_SHAMT), .SB(SB), .BLTZ(BLTZ),
    .R1_Used(R1_Used), .R2_Used(R2_Used));

  // Other names for the same wires on the sheet: OP_CODE[5:0] = OP

  // Notes on the sheet:
  //   运算器控制器，根据指令生成运算器功能选择信号
  //   控制信号生成，产生数据通路需要的其他控制信号
endmodule

// 运算器控制器
module \运算控制器自动生成  (
  input  OP0,
  input  OP1,
  input  OP2,
  input  OP3,
  input  OP4,
  input  OP5,
  input  F0,
  input  F1,
  input  F2,
  input  F3,
  input  F4,
  input  F5,
  output S0,
  output S1,
  output S2,
  output S3
);

  wire and_1_out, and_2_out, and_3_out, and_4_out, and_5_out, and_6_out, and_7_out, and_8_out, and_9_out,
       and_10_out, and_11_out, and_12_out, and_13_out, and_14_out, and_15_out, and_16_out, and_17_out,
       and_18_out, and_19_out, and_20_out, and_21_out, and_22_out, and_23_out, and_24_out, and_25_out,
       and_26_out, and_27_out, and_28_out, and_29_out, and_30_out, and_31_out, and_32_out, and_33_out,
       and_34_out, and_35_out, and_36_out, and_37_out, not_1_out, not_2_out, not_3_out, not_4_out, not_5_out,
       not_6_out, not_7_out, not_8_out, not_9_out, not_10_out, not_11_out, not_12_out, not_13_out,
       not_14_out, not_15_out, not_16_out, not_17_out, not_18_out, not_19_out, not_20_out, not_21_out,
       not_22_out, not_23_out, not_24_out, not_25_out, not_26_out, not_27_out, not_28_out, not_29_out,
       not_30_out, not_31_out, not_32_out, not_33_out, not_34_out, not_35_out, not_36_out, not_37_out,
       not_38_out, not_39_out, not_40_out, not_41_out, not_42_out, not_43_out, not_44_out, not_45_out,
       not_46_out, not_47_out, not_48_out, not_49_out, not_50_out, not_51_out, not_52_out, not_53_out,
       not_54_out, not_55_out, not_56_out, not_57_out, not_58_out, not_59_out, not_60_out, not_61_out,
       not_62_out, not_63_out, not_64_out, not_65_out, not_66_out, not_67_out, not_68_out, not_69_out,
       not_70_out, not_71_out, not_72_out, not_73_out, not_74_out, not_75_out, not_76_out, not_77_out,
       not_78_out, not_79_out, not_80_out, not_81_out, not_82_out, not_83_out, not_84_out, not_85_out,
       not_86_out, not_87_out, not_88_out, not_89_out, not_90_out, not_91_out, not_92_out, not_93_out,
       not_94_out, not_95_out, not_96_out, not_97_out, not_98_out, not_99_out, not_100_out, not_101_out,
       not_102_out, not_103_out, not_104_out, not_105_out, not_106_out, not_107_out, not_108_out,
       not_109_out, not_110_out, not_111_out, not_112_out, not_113_out, not_114_out, not_115_out,
       not_116_out, not_117_out, not_118_out, not_119_out, not_120_out, not_121_out, not_122_out,
       not_123_out, not_124_out, not_125_out, not_126_out, not_127_out, not_128_out, not_129_out,
       not_130_out, not_131_out, not_132_out, not_133_out, not_134_out, not_135_out, not_136_out,
       not_137_out, not_138_out, not_139_out, not_140_out, not_141_out, not_142_out, not_143_out,
       not_144_out, not_145_out, not_146_out, not_147_out, not_148_out, not_149_out, not_150_out,
       not_151_out, not_152_out, not_153_out, not_154_out, not_155_out, not_156_out, not_157_out,
       not_158_out, not_159_out, not_160_out, not_161_out, not_162_out, not_163_out, not_164_out,
       not_165_out, not_166_out, not_167_out, not_168_out, not_169_out, not_170_out, not_171_out,
       not_172_out, not_173_out, not_174_out, not_175_out, not_176_out, not_177_out, not_178_out,
       not_179_out, not_180_out, not_181_out, not_182_out, not_183_out, not_184_out, not_185_out,
       not_186_out, not_187_out, not_188_out, not_189_out, not_190_out, not_191_out, not_192_out,
       not_193_out, not_194_out, not_195_out, not_196_out, not_197_out, not_198_out, not_199_out,
       not_200_out, not_201_out, not_202_out, not_203_out, not_204_out, not_205_out, not_206_out,
       not_207_out, not_208_out, not_209_out, not_210_out, not_211_out, not_212_out, not_213_out,
       not_214_out, not_215_out, not_216_out, not_217_out, not_218_out, not_219_out, not_220_out,
       not_221_out, not_222_out, not_223_out, not_224_out, not_225_out, not_226_out, not_227_out,
       not_228_out, not_229_out, not_230_out, not_231_out, not_232_out, not_233_out, not_234_out,
       not_235_out, not_236_out, not_237_out, not_238_out, not_239_out, not_240_out, not_241_out,
       not_242_out, not_243_out, not_244_out, not_245_out, not_246_out, not_247_out, not_248_out,
       not_249_out, not_250_out, not_251_out, not_252_out;

  not not_1 (not_1_out, OP5);
  not not_2 (not_2_out, OP4);
  not not_3 (not_3_out, OP3);
  not not_4 (not_4_out, OP2);
  not not_5 (not_5_out, OP1);
  not not_6 (not_6_out, OP0);
  not not_7 (not_7_out, F5);
  not not_8 (not_8_out, F4);
  not not_9 (not_9_out, F3);
  not not_10 (not_10_out, F2);
  not not_11 (not_11_out, OP5);
  not not_12 (not_12_out, OP4);
  not not_13 (not_13_out, OP3);
  not not_14 (not_14_out, OP2);
  not not_15 (not_15_out, OP1);
  not not_16 (not_16_out, OP0);
  not not_17 (not_17_out, F4);
  not not_18 (not_18_out, F3);
  not not_19 (not_19_out, F2);
  not not_20 (not_20_out, F1);
  not not_21 (not_21_out, F0);
  not not_22 (not_22_out, OP5);
  not not_23 (not_23_out, OP4);
  not not_24 (not_24_out, OP3);
  not not_25 (not_25_out, OP2);
  not not_26 (not_26_out, OP1);
  not not_27 (not_27_out, OP0);
  not not_28 (not_28_out, F4);
  not not_29 (not_29_out, F3);
  not not_30 (not_30_out, F2);
  not not_31 (not_31_out, F1);
  not not_32 (not_32_out, OP5);
  not not_33 (not_33_out, OP4);
  not not_34 (not_34_out, OP3);
  not not_35 (not_35_out, OP2);
  not not_36 (not_36_out, OP1);
  not not_37 (not_37_out, OP0);
  not not_38 (not_38_out, F4);
  not not_39 (not_39_out, F3);
  not not_40 (not_40_out, F1);
  not not_41 (not_41_out, F0);
  not not_42 (not_42_out, OP5);
  not not_43 (not_43_out, OP4);
  not not_44 (not_44_out, OP3);
  not not_45 (not_45_out, OP2);
  not not_46 (not_46_out, OP1);
  not not_47 (not_47_out, OP0);
  not not_48 (not_48_out, F4);
  not not_49 (not_49_out, F2);
  not not_50 (not_50_out, F0);
  not not_51 (not_51_out, OP5);
  not not_52 (not_52_out, OP4);
  not not_53 (not_53_out, OP2);
  not not_54 (not_54_out, OP1);
  not not_55 (not_55_out, OP0);
  not not_56 (not_56_out, OP5);
  not not_57 (not_57_out, OP4);
  not not_58 (not_58_out, OP1);
  not not_59 (not_59_out, OP0);
  not not_60 (not_60_out, OP5);
  not not_61 (not_61_out, OP4);
  not not_62 (not_62_out, OP2);
  not not_63 (not_63_out, OP1);
  not not_64 (not_64_out, OP5);
  not not_65 (not_65_out, OP4);
  not not_66 (not_66_out, OP2);
  not not_67 (not_67_out, OP0);
  not not_68 (not_68_out, OP4);
  not not_69 (not_69_out, OP3);
  not not_70 (not_70_out, OP2);
  not not_71 (not_71_out, OP4);
  not not_72 (not_72_out, OP2);
  not not_73 (not_73_out, OP5);
  not not_74 (not_74_out, OP4);
  not not_75 (not_75_out, OP0);
  not not_76 (not_76_out, OP5);
  not not_77 (not_77_out, OP4);
  not not_78 (not_78_out, OP3);
  not not_79 (not_79_out, OP2);
  not not_80 (not_80_out, OP1);
  not not_81 (not_81_out, OP0);
  not not_82 (not_82_out, F5);
  not not_83 (not_83_out, F4);
  not not_84 (not_84_out, F3);
  not not_85 (not_85_out, F2);
  not not_86 (not_86_out, F0);
  not not_87 (not_87_out, OP5);
  not not_88 (not_88_out, OP4);
  not not_89 (not_89_out, OP3);
  not not_90 (not_90_out, OP2);
  not not_91 (not_91_out, OP1);
  not not_92 (not_92_out, OP0);
  not not_93 (not_93_out, F4);
  not not_94 (not_94_out, F3);
  not not_95 (not_95_out, F2);
  not not_96 (not_96_out, F0);
  not not_97 (not_97_out, OP5);
  not not_98 (not_98_out, OP4);
  not not_99 (not_99_out, OP3);
  not not_100 (not_100_out, OP2);
  not not_101 (not_101_out, OP1);
  not not_102 (not_102_out, OP0);
  not not_103 (not_103_out, F4);
  not not_104 (not_104_out, F3);
  not not_105 (not_105_out, F1);
  not not_106 (not_106_out, F0);
  not not_107 (not_107_out, OP5);
  not not_108 (not_108_out, OP4);
  not not_109 (not_109_out, OP3);
  not not_110 (not_110_out, OP2);
  not not_111 (not_111_out, OP1);
  not not_112 (not_112_out, OP0);
  not not_113 (not_113_out, F4);
  not not_114 (not_114_out, F3);
  not not_115 (not_115_out, OP5);
  not not_116 (not_116_out, OP4);
  not not_117 (not_117_out, OP3);
  not not_118 (not_118_out, OP2);
  not not_119 (not_119_out, OP1);
  not not_120 (not_120_out, OP0);
  not not_121 (not_121_out, F4);
  not not_122 (not_122_out, F2);
  not not_123 (not_123_out, F0);
  not not_124 (not_124_out, OP5);
  not not_125 (not_125_out, OP4);
  not not_126 (not_126_out, OP1);
  not not_127 (not_127_out, OP0);
  not not_128 (not_128_out, OP5);
  not not_129 (not_129_out, OP4);
  not not_130 (not_130_out, OP2);
  not not_131 (not_131_out, OP0);
  not not_132 (not_132_out, OP5);
  not not_133 (not_133_out, OP4);
  not not_134 (not_134_out, OP3);
  not not_135 (not_135_out, OP2);
  not not_136 (not_136_out, OP1);
  not not_137 (not_137_out, OP0);
  not not_138 (not_138_out, F5);
  not not_139 (not_139_out, F4);
  not not_140 (not_140_out, F3);
  not not_141 (not_141_out, F0);
  not not_142 (not_142_out, OP5);
  not not_143 (not_143_out, OP4);
  not not_144 (not_144_out, OP3);
  not not_145 (not_145_out, OP2);
  not not_146 (not_146_out, OP1);
  not not_147 (not_147_out, OP0);
  not not_148 (not_148_out, F4);
  not not_149 (not_149_out, F3);
  not not_150 (not_150_out, F2);
  not not_151 (not_151_out, F1);
  not not_152 (not_152_out, F0);
  not not_153 (not_153_out, OP5);
  not not_154 (not_154_out, OP4);
  not not_155 (not_155_out, OP3);
  not not_156 (not_156_out, OP2);
  not not_157 (not_157_out, OP1);
  not not_158 (not_158_out, OP0);
  not not_159 (not_159_out, F4);
  not not_160 (not_160_out, F3);
  not not_161 (not_161_out, F2);
  not not_162 (not_162_out, F1);
  not not_163 (not_163_out, OP5);
  not not_164 (not_164_out, OP4);
  not not_165 (not_165_out, OP3);
  not not_166 (not_166_out, OP2);
  not not_167 (not_167_out, OP1);
  not not_168 (not_168_out, OP0);
  not not_169 (not_169_out, F4);
  not not_170 (not_170_out, F3);
  not not_171 (not_171_out, F2);
  not not_172 (not_172_out, F0);
  not not_173 (not_173_out, OP5);
  not not_174 (not_174_out, OP4);
  not not_175 (not_175_out, OP3);
  not not_176 (not_176_out, OP2);
  not not_177 (not_177_out, OP1);
  not not_178 (not_178_out, OP0);
  not not_179 (not_179_out, F4);
  not not_180 (not_180_out, F3);
  not not_181 (not_181_out, F1);
  not not_182 (not_182_out, F0);
  not not_183 (not_183_out, OP5);
  not not_184 (not_184_out, OP4);
  not not_185 (not_185_out, OP3);
  not not_186 (not_186_out, OP2);
  not not_187 (not_187_out, OP1);
  not not_188 (not_188_out, OP0);
  not not_189 (not_189_out, F4);
  not not_190 (not_190_out, F2);
  not not_191 (not_191_out, OP5);
  not not_192 (not_192_out, OP4);
  not not_193 (not_193_out, OP2);
  not not_194 (not_194_out, OP1);
  not not_195 (not_195_out, OP0);
  not not_196 (not_196_out, OP5);
  not not_197 (not_197_out, OP4);
  not not_198 (not_198_out, OP1);
  not not_199 (not_199_out, OP0);
  not not_200 (not_200_out, OP5);
  not not_201 (not_201_out, OP4);
  not not_202 (not_202_out, OP2);
  not not_203 (not_203_out, OP1);
  not not_204 (not_204_out, OP4);
  not not_205 (not_205_out, OP3);
  not not_206 (not_206_out, OP2);
  not not_207 (not_207_out, OP4);
  not not_208 (not_208_out, OP2);
  not not_209 (not_209_out, OP5);
  not not_210 (not_210_out, OP4);
  not not_211 (not_211_out, OP3);
  not not_212 (not_212_out, OP2);
  not not_213 (not_213_out, OP1);
  not not_214 (not_214_out, OP0);
  not not_215 (not_215_out, F4);
  not not_216 (not_216_out, F3);
  not not_217 (not_217_out, F1);
  not not_218 (not_218_out, OP5);
  not not_219 (not_219_out, OP4);
  not not_220 (not_220_out, OP3);
  not not_221 (not_221_out, OP2);
  not not_222 (not_222_out, OP1);
  not not_223 (not_223_out, OP0);
  not not_224 (not_224_out, F4);
  not not_225 (not_225_out, F3);
  not not_226 (not_226_out, OP5);
  not not_227 (not_227_out, OP4);
  not not_228 (not_228_out, OP3);
  not not_229 (not_229_out, OP2);
  not not_230 (not_230_out, OP1);
  not not_231 (not_231_out, OP0);
  not not_232 (not_232_out, F4);
  not not_233 (not_233_out, F2);
  not not_234 (not_234_out, F0);
  not not_235 (not_235_out, OP5);
  not not_236 (not_236_out, OP4);
  not not_237 (not_237_out, OP3);
  not not_238 (not_238_out, OP2);
  not not_239 (not_239_out, OP1);
  not not_240 (not_240_out, OP0);
  not not_241 (not_241_out, F4);
  not not_242 (not_242_out, F2);
  not not_243 (not_243_out, OP5);
  not not_244 (not_244_out, OP4);
  not not_245 (not_245_out, OP2);
  not not_246 (not_246_out, OP0);
  not not_247 (not_247_out, OP5);
  not not_248 (not_248_out, OP4);
  not not_249 (not_249_out, OP1);
  not not_250 (not_250_out, OP5);
  not not_251 (not_251_out, OP4);
  not not_252 (not_252_out, OP0);
  and and_1 (and_1_out, not_1_out, not_2_out, not_3_out, not_4_out, not_5_out, not_6_out, not_7_out, not_8_out, not_9_out, not_10_out, F1, F0);
  and and_2 (and_2_out, not_11_out, not_12_out, not_13_out, not_14_out, not_15_out, not_16_out, F5, not_17_out, not_18_out, not_19_out, not_20_out, not_21_out);
  and and_3 (and_3_out, not_22_out, not_23_out, not_24_out, not_25_out, not_26_out, not_27_out, F5, not_28_out, not_29_out, not_30_out, not_31_out, F0);
  and and_4 (and_4_out, not_32_out, not_33_out, not_34_out, not_35_out, not_36_out, not_37_out, F5, not_38_out, not_39_out, F2, not_40_out, not_41_out);
  and and_5 (and_5_out, not_42_out, not_43_out, not_44_out, not_45_out, not_46_out, not_47_out, F5, not_48_out, F3, not_49_out, F1, not_50_out);
  and and_6 (and_6_out, not_51_out, not_52_out, OP3, not_53_out, not_54_out, not_55_out);
  and and_7 (and_7_out, not_56_out, not_57_out, OP3, OP2, not_58_out, not_59_out);
  and and_8 (and_8_out, not_60_out, not_61_out, OP3, not_62_out, not_63_out, OP0);
  and and_9 (and_9_out, not_64_out, not_65_out, OP3, not_66_out, OP1, not_67_out);
  and and_10 (and_10_out, OP5, not_68_out, not_69_out, not_70_out, OP1, OP0);
  and and_11 (and_11_out, OP5, not_71_out, OP3, not_72_out, OP1, OP0);
  and and_12 (and_12_out, not_73_out, not_74_out, OP3, OP2, OP1, not_75_out);
  and and_13 (and_13_out, not_76_out, not_77_out, not_78_out, not_79_out, not_80_out, not_81_out, not_82_out, not_83_out, not_84_out, not_85_out, F1, not_86_out);
  and and_14 (and_14_out, not_87_out, not_88_out, not_89_out, not_90_out, not_91_out, not_92_out, F5, not_93_out, not_94_out, not_95_out, F1, not_96_out);
  and and_15 (and_15_out, not_97_out, not_98_out, not_99_out, not_100_out, not_101_out, not_102_out, F5, not_103_out, not_104_out, F2, not_105_out, not_106_out);
  and and_16 (and_16_out, not_107_out, not_108_out, not_109_out, not_110_out, not_111_out, not_112_out, F5, not_113_out, not_114_out, F2, F1, F0);
  and and_17 (and_17_out, not_115_out, not_116_out, not_117_out, not_118_out, not_119_out, not_120_out, F5, not_121_out, F3, not_122_out, F1, not_123_out);
  and and_18 (and_18_out, not_124_out, not_125_out, OP3, OP2, not_126_out, not_127_out);
  and and_19 (and_19_out, not_128_out, not_129_out, OP3, not_130_out, OP1, not_131_out);
  and and_20 (and_20_out, not_132_out, not_133_out, not_134_out, not_135_out, not_136_out, not_137_out, not_138_out, not_139_out, not_140_out, F2, F1, not_141_out);
  and and_21 (and_21_out, not_142_out, not_143_out, not_144_out, not_145_out, not_146_out, not_147_out, F5, not_148_out, not_149_out, not_150_out, not_151_out, not_152_out);
  and and_22 (and_22_out, not_153_out, not_154_out, not_155_out, not_156_out, not_157_out, not_158_out, F5, not_159_out, not_160_out, not_161_out, not_162_out, F0);
  and and_23 (and_23_out, not_163_out, not_164_out, not_165_out, not_166_out, not_167_out, not_168_out, F5, not_169_out, not_170_out, not_171_out, F1, not_172_out);
  and and_24 (and_24_out, not_173_out, not_174_out, not_175_out, not_176_out, not_177_out, not_178_out, F5, not_179_out, not_180_out, F2, not_181_out, not_182_out);
  and and_25 (and_25_out, not_183_out, not_184_out, not_185_out, not_186_out, not_187_out, not_188_out, F5, not_189_out, F3, not_190_out, F1, F0);
  and and_26 (and_26_out, not_191_out, not_192_out, OP3, not_193_out, not_194_out, not_195_out);
  and and_27 (and_27_out, not_196_out, not_197_out, OP3, OP2, not_198_out, not_199_out);
  and and_28 (and_28_out, not_200_out, not_201_out, OP3, not_202_out, not_203_out, OP0);
  and and_29 (and_29_out, OP5, not_204_out, not_205_out, not_206_out, OP1, OP0);
  and and_30 (and_30_out, OP5, not_207_out, OP3, not_208_out, OP1, OP0);
  and and_31 (and_31_out, not_209_out, not_210_out, not_211_out, not_212_out, not_213_out, not_214_out, F5, not_215_out, not_216_out, F2, not_217_out, F0);
  and and_32 (and_32_out, not_218_out, not_219_out, not_220_out, not_221_out, not_222_out, not_223_out, F5, not_224_out, not_225_out, F2, F1, F0);
  and and_33 (and_33_out, not_226_out, not_227_out, not_228_out, not_229_out, not_230_out, not_231_out, F5, not_232_out, F3, not_233_out, F1, not_234_out);
  and and_34 (and_34_out, not_235_out, not_236_out, not_237_out, not_238_out, not_239_out, not_240_out, F5, not_241_out, F3, not_242_out, F1, F0);
  and and_35 (and_35_out, not_243_out, not_244_out, OP3, not_245_out, OP1, not_246_out);
  and and_36 (and_36_out, not_247_out, not_248_out, OP3, OP2, not_249_out, OP0);
  and and_37 (and_37_out, not_250_out, not_251_out, OP3, OP2, OP1, not_252_out);
  or or_1 (S1, and_13_out, and_14_out, and_15_out, and_16_out, and_17_out, and_18_out, and_19_out, and_20_out);
  or or_2 (S2, and_21_out, and_22_out, and_23_out, and_24_out, and_25_out, and_26_out, and_27_out, and_28_out, and_29_out, and_30_out);
  or or_3 (S3, and_31_out, and_32_out, and_33_out, and_34_out, and_35_out, and_36_out, and_37_out);
  or or_4 (S0, and_1_out, and_2_out, and_3_out, and_4_out, and_5_out, and_6_out, and_7_out, and_8_out, and_9_out, and_10_out, and_11_out, and_12_out);
endmodule

// 控制信号生成
module \控制信号自动生成  (
  input  OP0,
  input  OP1,
  input  OP2,
  input  OP3,
  input  OP4,
  input  OP5,
  input  F0,
  input  F1,
  input  F2,
  input  F3,
  input  F4,
  input  F5,
  output MemToReg,
  output MemWrite,
  output ALU_SRC,
  output RegWrite,
  output SysCALL,
  output SignedExt,
  output RegDst,
  output BEQ,
  output BNE,
  output JR,
  output JUMP,
  output JAL,
  output RS_SHAMT,
  output SB,
  output BLTZ,
  output R1_Used,
  output R2_Used
);

  wire and_2_out, and_3_out, and_4_out, and_5_out, and_6_out, and_7_out, and_8_out, and_9_out, and_10_out,
       and_11_out, and_12_out, and_13_out, and_14_out, and_15_out, and_16_out, and_17_out, and_18_out,
       and_19_out, and_20_out, and_21_out, and_22_out, and_23_out, and_24_out, and_25_out, and_26_out,
       and_27_out, and_28_out, and_29_out, and_30_out, and_31_out, and_32_out, and_34_out, and_35_out,
       and_36_out, and_37_out, and_38_out, and_39_out, and_40_out, and_41_out, and_42_out, and_43_out,
       and_44_out, and_45_out, and_46_out, and_47_out, and_48_out, and_49_out, and_50_out, and_51_out,
       and_52_out, and_61_out, and_62_out, and_63_out, and_64_out, and_65_out, and_66_out, and_67_out,
       and_68_out, and_69_out, and_70_out, and_71_out, and_72_out, and_73_out, and_74_out, and_75_out,
       and_76_out, and_77_out, and_78_out, and_79_out, and_80_out, and_81_out, and_82_out, and_83_out,
       and_84_out, and_85_out, and_86_out, and_87_out, and_88_out, and_89_out, and_90_out, and_91_out,
       and_92_out, and_93_out, and_94_out, and_95_out, and_96_out, and_97_out, and_98_out, and_99_out,
       and_100_out, not_1_out, not_2_out, not_3_out, not_4_out, not_5_out, not_6_out, not_7_out, not_8_out,
       not_9_out, not_10_out, not_11_out, not_12_out, not_13_out, not_14_out, not_15_out, not_16_out,
       not_17_out, not_18_out, not_19_out, not_20_out, not_21_out, not_22_out, not_23_out, not_24_out,
       not_25_out, not_26_out, not_27_out, not_28_out, not_29_out, not_30_out, not_31_out, not_32_out,
       not_33_out, not_34_out, not_35_out, not_36_out, not_37_out, not_38_out, not_39_out, not_40_out,
       not_41_out, not_42_out, not_43_out, not_44_out, not_45_out, not_46_out, not_47_out, not_48_out,
       not_49_out, not_50_out, not_51_out, not_52_out, not_53_out, not_54_out, not_55_out, not_56_out,
       not_57_out, not_58_out, not_59_out, not_60_out, not_61_out, not_62_out, not_63_out, not_64_out,
       not_65_out, not_66_out, not_67_out, not_68_out, not_69_out, not_70_out, not_71_out, not_72_out,
       not_73_out, not_74_out, not_75_out, not_76_out, not_77_out, not_78_out, not_79_out, not_80_out,
       not_81_out, not_82_out, not_83_out, not_84_out, not_85_out, not_86_out, not_87_out, not_88_out,
       not_89_out, not_90_out, not_91_out, not_92_out, not_93_out, not_94_out, not_95_out, not_96_out,
       not_97_out, not_98_out, not_99_out, not_100_out, not_101_out, not_102_out, not_103_out, not_104_out,
       not_105_out, not_106_out, not_107_out, not_108_out, not_109_out, not_110_out, not_111_out,
       not_112_out, not_113_out, not_114_out, not_115_out, not_116_out, not_117_out, not_118_out,
       not_119_out, not_120_out, not_121_out, not_122_out, not_123_out, not_124_out, not_125_out,
       not_126_out, not_127_out, not_128_out, not_129_out, not_130_out, not_131_out, not_132_out,
       not_133_out, not_134_out, not_135_out, not_136_out, not_137_out, not_138_out, not_139_out,
       not_140_out, not_141_out, not_142_out, not_143_out, not_144_out, not_145_out, not_146_out,
       not_147_out, not_148_out, not_149_out, not_150_out, not_151_out, not_152_out, not_153_out,
       not_154_out, not_155_out, not_156_out, not_157_out, not_158_out, not_159_out, not_160_out,
       not_161_out, not_162_out, not_163_out, not_164_out, not_165_out, not_166_out, not_167_out,
       not_168_out, not_169_out, not_170_out, not_171_out, not_172_out, not_173_out, not_174_out,
       not_175_out, not_176_out, not_177_out, not_178_out, not_179_out, not_180_out, not_181_out,
       not_182_out, not_183_out, not_184_out, not_185_out, not_186_out, not_187_out, not_188_out,
       not_189_out, not_190_out, not_191_out, not_192_out, not_193_out, not_194_out, not_195_out,
       not_196_out, not_197_out, not_198_out, not_199_out, not_200_out, not_201_out, not_202_out,
       not_203_out, not_204_out, not_205_out, not_206_out, not_207_out, not_208_out, not_209_out,
       not_210_out, not_211_out, not_212_out, not_213_out, not_214_out, not_215_out, not_216_out,
       not_217_out, not_218_out, not_219_out, not_220_out, not_221_out, not_222_out, not_223_out,
       not_224_out, not_225_out, not_226_out, not_227_out, not_228_out, not_229_out, not_230_out,
       not_231_out, not_232_out, not_233_out, not_234_out, not_235_out, not_236_out, not_237_out,
       not_238_out, not_239_out, not_240_out, not_241_out, not_242_out, not_243_out, not_244_out,
       not_245_out, not_246_out, not_247_out, not_248_out, not_249_out, not_250_out, not_251_out,
       not_252_out, not_253_out, not_254_out, not_255_out, not_256_out, not_257_out, not_258_out,
       not_259_out, not_260_out, not_261_out, not_262_out, not_263_out, not_264_out, not_265_out,
       not_266_out, not_267_out, not_268_out, not_269_out, not_270_out, not_271_out, not_272_out,
       not_273_out, not_274_out, not_275_out, not_276_out, not_277_out, not_278_out, not_279_out,
       not_280_out, not_281_out, not_282_out, not_283_out, not_284_out, not_285_out, not_286_out,
       not_287_out, not_288_out, not_289_out, not_290_out, not_291_out, not_292_out, not_293_out,
       not_294_out, not_295_out, not_296_out, not_297_out, not_298_out, not_299_out, not_300_out,
       not_301_out, not_302_out, not_303_out, not_304_out, not_305_out, not_306_out, not_307_out,
       not_308_out, not_309_out, not_310_out, not_311_out, not_312_out, not_313_out, not_314_out,
       not_315_out, not_316_out, not_317_out, not_318_out, not_319_out, not_320_out, not_321_out,
       not_322_out, not_323_out, not_324_out, not_325_out, not_326_out, not_327_out, not_328_out,
       not_329_out, not_330_out, not_331_out, not_332_out, not_333_out, not_334_out, not_335_out,
       not_336_out, not_337_out, not_338_out, not_339_out, not_340_out, not_341_out, not_342_out,
       not_343_out, not_344_out, not_345_out, not_346_out, not_347_out, not_348_out, not_349_out,
       not_350_out, not_351_out, not_352_out, not_353_out, not_354_out, not_355_out, not_356_out,
       not_357_out, not_358_out, not_359_out, not_360_out, not_361_out, not_362_out, not_363_out,
       not_364_out, not_365_out, not_366_out, not_367_out, not_368_out, not_369_out, not_370_out,
       not_371_out, not_372_out, not_373_out, not_374_out, not_375_out, not_376_out, not_377_out,
       not_378_out, not_379_out, not_380_out, not_381_out, not_382_out, not_383_out, not_384_out,
       not_385_out, not_386_out, not_387_out, not_388_out, not_389_out, not_390_out, not_391_out,
       not_392_out, not_393_out, not_394_out, not_395_out, not_396_out, not_397_out, not_398_out,
       not_399_out, not_400_out, not_401_out, not_402_out, not_403_out, not_404_out, not_405_out,
       not_406_out, not_407_out, not_408_out, not_409_out, not_410_out, not_411_out, not_412_out,
       not_413_out, not_414_out, not_415_out, not_416_out, not_417_out, not_418_out, not_419_out,
       not_420_out, not_421_out, not_422_out, not_423_out, not_424_out, not_425_out, not_426_out,
       not_427_out, not_428_out, not_429_out, not_430_out, not_431_out, not_432_out, not_433_out,
       not_434_out, not_435_out, not_436_out, not_437_out, not_438_out, not_439_out, not_440_out,
       not_441_out, not_442_out, not_443_out, not_444_out, not_445_out, not_446_out, not_447_out,
       not_448_out, not_449_out, not_450_out, not_451_out, not_452_out, not_453_out, not_454_out,
       not_455_out, not_456_out, not_457_out, not_458_out, not_459_out, not_460_out, not_461_out,
       not_462_out, not_463_out, not_464_out, not_465_out, not_466_out, not_467_out, not_468_out,
       not_469_out, not_470_out, not_471_out, not_472_out, not_473_out, not_474_out, not_475_out,
       not_476_out, not_477_out, not_478_out, not_479_out, not_480_out, not_481_out, not_482_out,
       not_483_out, not_484_out, not_485_out, not_486_out, not_487_out, not_488_out, not_489_out,
       not_490_out, not_491_out, not_492_out, not_493_out, not_494_out, not_495_out, not_496_out,
       not_497_out, not_498_out, not_499_out, not_500_out, not_501_out, not_502_out, not_503_out,
       not_504_out, not_505_out, not_506_out, not_507_out, not_508_out, not_509_out, not_510_out,
       not_511_out, not_512_out, not_513_out, not_514_out, not_515_out, not_516_out, not_517_out,
       not_518_out, not_519_out, not_520_out, not_521_out, not_522_out, not_523_out, not_524_out,
       not_525_out, not_526_out, not_527_out, not_528_out, not_529_out, not_530_out, not_531_out,
       not_532_out, not_533_out, not_534_out, not_535_out, not_536_out, not_537_out, not_538_out,
       not_539_out, not_540_out, not_541_out, not_542_out, not_543_out, not_544_out, not_545_out,
       not_546_out, not_547_out, not_548_out, not_549_out, not_550_out, not_551_out, not_552_out,
       not_553_out, not_554_out, not_555_out, not_556_out, not_557_out, not_558_out, not_559_out,
       not_560_out, not_561_out, not_562_out, not_563_out, not_564_out, not_565_out, not_566_out,
       not_567_out, not_568_out, not_569_out, not_570_out, not_571_out, not_572_out, not_573_out,
       not_574_out, not_575_out, not_576_out, not_577_out, not_578_out, not_579_out, not_580_out,
       not_581_out, not_582_out, not_583_out, not_584_out, not_585_out, not_586_out, not_587_out,
       not_588_out, not_589_out, not_590_out, not_591_out, not_592_out, not_593_out, not_594_out,
       not_595_out, not_596_out, not_597_out, not_598_out, not_599_out, not_600_out, not_601_out,
       not_602_out, not_603_out, not_604_out, not_605_out, not_606_out, not_607_out, not_608_out,
       not_609_out, not_610_out, not_611_out, not_612_out, not_613_out, not_614_out, not_615_out,
       not_616_out, not_617_out, not_618_out, not_619_out, not_620_out, not_621_out, not_622_out,
       not_623_out, not_624_out, not_625_out, not_626_out, not_627_out, not_628_out, not_629_out,
       not_630_out, not_631_out, not_632_out, not_633_out, not_634_out, not_635_out, not_636_out,
       not_637_out, not_638_out, not_639_out, not_640_out, not_641_out, not_642_out, not_643_out,
       not_644_out, not_645_out, not_646_out, not_647_out, not_648_out, not_649_out, not_650_out,
       not_651_out, not_652_out, not_653_out, not_654_out, not_655_out, not_656_out, not_657_out,
       not_658_out, not_659_out, not_660_out, not_661_out, not_662_out, not_663_out, not_664_out,
       not_665_out, not_666_out, not_667_out, not_668_out, not_669_out, not_670_out, not_671_out,
       not_672_out, not_673_out, not_674_out, not_675_out, not_676_out, not_677_out, not_678_out;

  not not_1 (not_1_out, OP4);
  not not_2 (not_2_out, OP3);
  not not_3 (not_3_out, OP2);
  not not_4 (not_4_out, OP0);
  not not_5 (not_5_out, OP1);
  not not_6 (not_6_out, OP2);
  not not_7 (not_7_out, OP4);
  not not_8 (not_8_out, OP2);
  not not_9 (not_9_out, OP4);
  not not_10 (not_10_out, OP5);
  not not_11 (not_11_out, OP4);
  not not_12 (not_12_out, OP2);
  not not_13 (not_13_out, OP1);
  not not_14 (not_14_out, OP0);
  not not_15 (not_15_out, OP5);
  not not_16 (not_16_out, OP4);
  not not_17 (not_17_out, OP1);
  not not_18 (not_18_out, OP0);
  not not_19 (not_19_out, OP5);
  not not_20 (not_20_out, OP4);
  not not_21 (not_21_out, OP2);
  not not_22 (not_22_out, OP1);
  not not_23 (not_23_out, OP5);
  not not_24 (not_24_out, OP4);
  not not_25 (not_25_out, OP2);
  not not_26 (not_26_out, OP0);
  not not_27 (not_27_out, OP5);
  not not_28 (not_28_out, OP4);
  not not_29 (not_29_out, OP1);
  not not_30 (not_30_out, OP4);
  not not_31 (not_31_out, OP3);
  not not_32 (not_32_out, OP2);
  not not_33 (not_33_out, OP4);
  not not_34 (not_34_out, OP2);
  not not_35 (not_35_out, OP5);
  not not_36 (not_36_out, OP4);
  not not_37 (not_37_out, OP0);
  not not_38 (not_38_out, OP4);
  not not_39 (not_39_out, OP2);
  not not_40 (not_40_out, OP1);
  not not_41 (not_41_out, OP0);
  not not_42 (not_42_out, OP5);
  not not_43 (not_43_out, OP4);
  not not_44 (not_44_out, OP3);
  not not_45 (not_45_out, OP2);
  not not_46 (not_46_out, OP1);
  not not_47 (not_47_out, OP0);
  not not_48 (not_48_out, F5);
  not not_49 (not_49_out, F4);
  not not_50 (not_50_out, F3);
  not not_51 (not_51_out, F2);
  not not_52 (not_52_out, F1);
  not not_53 (not_53_out, F0);
  not not_54 (not_54_out, OP5);
  not not_55 (not_55_out, OP4);
  not not_56 (not_56_out, OP3);
  not not_57 (not_57_out, OP2);
  not not_58 (not_58_out, OP1);
  not not_59 (not_59_out, OP0);
  not not_60 (not_60_out, F5);
  not not_61 (not_61_out, F4);
  not not_62 (not_62_out, F3);
  not not_63 (not_63_out, F2);
  not not_64 (not_64_out, OP5);
  not not_65 (not_65_out, OP4);
  not not_66 (not_66_out, OP3);
  not not_67 (not_67_out, OP2);
  not not_68 (not_68_out, OP1);
  not not_69 (not_69_out, OP0);
  not not_70 (not_70_out, F5);
  not not_71 (not_71_out, F4);
  not not_72 (not_72_out, F3);
  not not_73 (not_73_out, F2);
  not not_74 (not_74_out, F0);
  not not_75 (not_75_out, OP5);
  not not_76 (not_76_out, OP4);
  not not_77 (not_77_out, OP3);
  not not_78 (not_78_out, OP2);
  not not_79 (not_79_out, OP1);
  not not_80 (not_80_out, OP0);
  not not_81 (not_81_out, F4);
  not not_82 (not_82_out, F3);
  not not_83 (not_83_out, F2);
  not not_84 (not_84_out, F1);
  not not_85 (not_85_out, F0);
  not not_86 (not_86_out, OP5);
  not not_87 (not_87_out, OP4);
  not not_88 (not_88_out, OP3);
  not not_89 (not_89_out, OP2);
  not not_90 (not_90_out, OP1);
  not not_91 (not_91_out, OP0);
  not not_92 (not_92_out, F4);
  not not_93 (not_93_out, F3);
  not not_94 (not_94_out, F2);
  not not_95 (not_95_out, F1);
  not not_96 (not_96_out, OP5);
  not not_97 (not_97_out, OP4);
  not not_98 (not_98_out, OP3);
  not not_99 (not_99_out, OP2);
  not not_100 (not_100_out, OP1);
  not not_101 (not_101_out, OP0);
  not not_102 (not_102_out, F4);
  not not_103 (not_103_out, F3);
  not not_104 (not_104_out, F2);
  not not_105 (not_105_out, F0);
  not not_106 (not_106_out, OP5);
  not not_107 (not_107_out, OP4);
  not not_108 (not_108_out, OP3);
  not not_109 (not_109_out, OP2);
  not not_110 (not_110_out, OP1);
  not not_111 (not_111_out, OP0);
  not not_112 (not_112_out, F4);
  not not_113 (not_113_out, F3);
  not not_114 (not_114_out, F1);
  not not_115 (not_115_out, F0);
  not not_116 (not_116_out, OP5);
  not not_117 (not_117_out, OP4);
  not not_118 (not_118_out, OP3);
  not not_119 (not_119_out, OP2);
  not not_120 (not_120_out, OP1);
  not not_121 (not_121_out, OP0);
  not not_122 (not_122_out, F4);
  not not_123 (not_123_out, F3);
  not not_124 (not_124_out, F1);
  not not_125 (not_125_out, OP5);
  not not_126 (not_126_out, OP4);
  not not_127 (not_127_out, OP3);
  not not_128 (not_128_out, OP2);
  not not_129 (not_129_out, OP1);
  not not_130 (not_130_out, OP0);
  not not_131 (not_131_out, F4);
  not not_132 (not_132_out, F3);
  not not_133 (not_133_out, OP5);
  not not_134 (not_134_out, OP4);
  not not_135 (not_135_out, OP3);
  not not_136 (not_136_out, OP2);
  not not_137 (not_137_out, OP1);
  not not_138 (not_138_out, OP0);
  not not_139 (not_139_out, F4);
  not not_140 (not_140_out, F2);
  not not_141 (not_141_out, F0);
  not not_142 (not_142_out, OP5);
  not not_143 (not_143_out, OP4);
  not not_144 (not_144_out, OP3);
  not not_145 (not_145_out, OP2);
  not not_146 (not_146_out, OP1);
  not not_147 (not_147_out, OP0);
  not not_148 (not_148_out, F4);
  not not_149 (not_149_out, F2);
  not not_150 (not_150_out, OP5);
  not not_151 (not_151_out, OP4);
  not not_152 (not_152_out, OP3);
  not not_153 (not_153_out, OP2);
  not not_154 (not_154_out, OP5);
  not not_155 (not_155_out, OP4);
  not not_156 (not_156_out, OP2);
  not not_157 (not_157_out, OP1);
  not not_158 (not_158_out, OP0);
  not not_159 (not_159_out, OP5);
  not not_160 (not_160_out, OP4);
  not not_161 (not_161_out, OP1);
  not not_162 (not_162_out, OP0);
  not not_163 (not_163_out, OP5);
  not not_164 (not_164_out, OP4);
  not not_165 (not_165_out, OP2);
  not not_166 (not_166_out, OP1);
  not not_167 (not_167_out, OP5);
  not not_168 (not_168_out, OP4);
  not not_169 (not_169_out, OP2);
  not not_170 (not_170_out, OP0);
  not not_171 (not_171_out, OP5);
  not not_172 (not_172_out, OP4);
  not not_173 (not_173_out, OP1);
  not not_174 (not_174_out, OP4);
  not not_175 (not_175_out, OP3);
  not not_176 (not_176_out, OP2);
  not not_177 (not_177_out, OP5);
  not not_178 (not_178_out, OP4);
  not not_179 (not_179_out, OP3);
  not not_180 (not_180_out, OP2);
  not not_181 (not_181_out, OP1);
  not not_182 (not_182_out, OP0);
  not not_183 (not_183_out, F5);
  not not_184 (not_184_out, F4);
  not not_185 (not_185_out, F3);
  not not_186 (not_186_out, F0);
  not not_187 (not_187_out, OP5);
  not not_188 (not_188_out, OP4);
  not not_189 (not_189_out, OP0);
  not not_190 (not_190_out, OP5);
  not not_191 (not_191_out, OP4);
  not not_192 (not_192_out, OP3);
  not not_193 (not_193_out, OP2);
  not not_194 (not_194_out, OP1);
  not not_195 (not_195_out, OP0);
  not not_196 (not_196_out, F5);
  not not_197 (not_197_out, F4);
  not not_198 (not_198_out, F1);
  not not_199 (not_199_out, F0);
  not not_200 (not_200_out, OP5);
  not not_201 (not_201_out, OP4);
  not not_202 (not_202_out, OP2);
  not not_203 (not_203_out, OP1);
  not not_204 (not_204_out, OP0);
  not not_205 (not_205_out, OP5);
  not not_206 (not_206_out, OP4);
  not not_207 (not_207_out, OP2);
  not not_208 (not_208_out, OP1);
  not not_209 (not_209_out, OP5);
  not not_210 (not_210_out, OP4);
  not not_211 (not_211_out, OP2);
  not not_212 (not_212_out, OP0);
  not not_213 (not_213_out, OP4);
  not not_214 (not_214_out, OP3);
  not not_215 (not_215_out, OP2);
  not not_216 (not_216_out, OP4);
  not not_217 (not_217_out, OP2);
  not not_218 (not_218_out, OP4);
  not not_219 (not_219_out, OP2);
  not not_220 (not_220_out, OP1);
  not not_221 (not_221_out, OP0);
  not not_222 (not_222_out, OP5);
  not not_223 (not_223_out, OP4);
  not not_224 (not_224_out, OP3);
  not not_225 (not_225_out, OP2);
  not not_226 (not_226_out, OP1);
  not not_227 (not_227_out, OP0);
  not not_228 (not_228_out, F5);
  not not_229 (not_229_out, F4);
  not not_230 (not_230_out, F3);
  not not_231 (not_231_out, F2);
  not not_232 (not_232_out, F1);
  not not_233 (not_233_out, F0);
  not not_234 (not_234_out, OP5);
  not not_235 (not_235_out, OP4);
  not not_236 (not_236_out, OP3);
  not not_237 (not_237_out, OP2);
  not not_238 (not_238_out, OP1);
  not not_239 (not_239_out, OP0);
  not not_240 (not_240_out, F5);
  not not_241 (not_241_out, F4);
  not not_242 (not_242_out, F3);
  not not_243 (not_243_out, F2);
  not not_244 (not_244_out, OP5);
  not not_245 (not_245_out, OP4);
  not not_246 (not_246_out, OP3);
  not not_247 (not_247_out, OP2);
  not not_248 (not_248_out, OP1);
  not not_249 (not_249_out, OP0);
  not not_250 (not_250_out, F5);
  not not_251 (not_251_out, F4);
  not not_252 (not_252_out, F3);
  not not_253 (not_253_out, F2);
  not not_254 (not_254_out, F0);
  not not_255 (not_255_out, OP5);
  not not_256 (not_256_out, OP4);
  not not_257 (not_257_out, OP3);
  not not_258 (not_258_out, OP2);
  not not_259 (not_259_out, OP1);
  not not_260 (not_260_out, OP0);
  not not_261 (not_261_out, F4);
  not not_262 (not_262_out, F3);
  not not_263 (not_263_out, F2);
  not not_264 (not_264_out, F1);
  not not_265 (not_265_out, F0);
  not not_266 (not_266_out, OP5);
  not not_267 (not_267_out, OP4);
  not not_268 (not_268_out, OP3);
  not not_269 (not_269_out, OP2);
  not not_270 (not_270_out, OP1);
  not not_271 (not_271_out, OP0);
  not not_272 (not_272_out, F4);
  not not_273 (not_273_out, F3);
  not not_274 (not_274_out, F2);
  not not_275 (not_275_out, F1);
  not not_276 (not_276_out, OP5);
  not not_277 (not_277_out, OP4);
  not not_278 (not_278_out, OP3);
  not not_279 (not_279_out, OP2);
  not not_280 (not_280_out, OP1);
  not not_281 (not_281_out, OP0);
  not not_282 (not_282_out, F4);
  not not_283 (not_283_out, F3);
  not not_284 (not_284_out, F2);
  not not_285 (not_285_out, F0);
  not not_286 (not_286_out, OP5);
  not not_287 (not_287_out, OP4);
  not not_288 (not_288_out, OP3);
  not not_289 (not_289_out, OP2);
  not not_290 (not_290_out, OP1);
  not not_291 (not_291_out, OP0);
  not not_292 (not_292_out, F4);
  not not_293 (not_293_out, F3);
  not not_294 (not_294_out, F1);
  not not_295 (not_295_out, F0);
  not not_296 (not_296_out, OP5);
  not not_297 (not_297_out, OP4);
  not not_298 (not_298_out, OP3);
  not not_299 (not_299_out, OP2);
  not not_300 (not_300_out, OP1);
  not not_301 (not_301_out, OP0);
  not not_302 (not_302_out, F4);
  not not_303 (not_303_out, F3);
  not not_304 (not_304_out, F1);
  not not_305 (not_305_out, OP5);
  not not_306 (not_306_out, OP4);
  not not_307 (not_307_out, OP3);
  not not_308 (not_308_out, OP2);
  not not_309 (not_309_out, OP1);
  not not_310 (not_310_out, OP0);
  not not_311 (not_311_out, F4);
  not not_312 (not_312_out, F3);
  not not_313 (not_313_out, OP5);
  not not_314 (not_314_out, OP4);
  not not_315 (not_315_out, OP3);
  not not_316 (not_316_out, OP2);
  not not_317 (not_317_out, OP1);
  not not_318 (not_318_out, OP0);
  not not_319 (not_319_out, F4);
  not not_320 (not_320_out, F2);
  not not_321 (not_321_out, F0);
  not not_322 (not_322_out, OP5);
  not not_323 (not_323_out, OP4);
  not not_324 (not_324_out, OP3);
  not not_325 (not_325_out, OP2);
  not not_326 (not_326_out, OP1);
  not not_327 (not_327_out, OP0);
  not not_328 (not_328_out, F4);
  not not_329 (not_329_out, F2);
  not not_330 (not_330_out, OP5);
  not not_331 (not_331_out, OP4);
  not not_332 (not_332_out, OP3);
  not not_333 (not_333_out, OP2);
  not not_334 (not_334_out, OP1);
  not not_335 (not_335_out, OP0);
  not not_336 (not_336_out, F5);
  not not_337 (not_337_out, F4);
  not not_338 (not_338_out, F3);
  not not_339 (not_339_out, F0);
  not not_340 (not_340_out, OP5);
  not not_341 (not_341_out, OP4);
  not not_342 (not_342_out, OP0);
  not not_343 (not_343_out, OP5);
  not not_344 (not_344_out, OP4);
  not not_345 (not_345_out, OP3);
  not not_346 (not_346_out, OP1);
  not not_347 (not_347_out, OP0);
  not not_348 (not_348_out, OP5);
  not not_349 (not_349_out, OP4);
  not not_350 (not_350_out, OP3);
  not not_351 (not_351_out, OP1);
  not not_352 (not_352_out, OP5);
  not not_353 (not_353_out, OP4);
  not not_354 (not_354_out, OP3);
  not not_355 (not_355_out, OP2);
  not not_356 (not_356_out, OP1);
  not not_357 (not_357_out, OP0);
  not not_358 (not_358_out, F5);
  not not_359 (not_359_out, F4);
  not not_360 (not_360_out, F2);
  not not_361 (not_361_out, F1);
  not not_362 (not_362_out, F0);
  not not_363 (not_363_out, OP5);
  not not_364 (not_364_out, OP4);
  not not_365 (not_365_out, OP3);
  not not_366 (not_366_out, OP2);
  not not_367 (not_367_out, OP0);
  not not_368 (not_368_out, OP5);
  not not_369 (not_369_out, OP4);
  not not_370 (not_370_out, OP3);
  not not_371 (not_371_out, OP2);
  not not_372 (not_372_out, OP5);
  not not_373 (not_373_out, OP4);
  not not_374 (not_374_out, OP0);
  not not_375 (not_375_out, OP4);
  not not_376 (not_376_out, OP2);
  not not_377 (not_377_out, OP1);
  not not_378 (not_378_out, OP0);
  not not_379 (not_379_out, OP5);
  not not_380 (not_380_out, OP4);
  not not_381 (not_381_out, OP3);
  not not_382 (not_382_out, OP2);
  not not_383 (not_383_out, OP1);
  not not_384 (not_384_out, OP5);
  not not_385 (not_385_out, OP4);
  not not_386 (not_386_out, OP3);
  not not_387 (not_387_out, OP2);
  not not_388 (not_388_out, OP1);
  not not_389 (not_389_out, OP0);
  not not_390 (not_390_out, F4);
  not not_391 (not_391_out, F3);
  not not_392 (not_392_out, F2);
  not not_393 (not_393_out, F1);
  not not_394 (not_394_out, F0);
  not not_395 (not_395_out, OP5);
  not not_396 (not_396_out, OP4);
  not not_397 (not_397_out, OP3);
  not not_398 (not_398_out, OP2);
  not not_399 (not_399_out, OP1);
  not not_400 (not_400_out, OP0);
  not not_401 (not_401_out, F4);
  not not_402 (not_402_out, F3);
  not not_403 (not_403_out, F2);
  not not_404 (not_404_out, F1);
  not not_405 (not_405_out, OP5);
  not not_406 (not_406_out, OP4);
  not not_407 (not_407_out, OP3);
  not not_408 (not_408_out, OP2);
  not not_409 (not_409_out, OP1);
  not not_410 (not_410_out, OP0);
  not not_411 (not_411_out, F4);
  not not_412 (not_412_out, F3);
  not not_413 (not_413_out, F2);
  not not_414 (not_414_out, F0);
  not not_415 (not_415_out, OP5);
  not not_416 (not_416_out, OP4);
  not not_417 (not_417_out, OP3);
  not not_418 (not_418_out, OP2);
  not not_419 (not_419_out, OP1);
  not not_420 (not_420_out, OP0);
  not not_421 (not_421_out, F4);
  not not_422 (not_422_out, F3);
  not not_423 (not_423_out, F1);
  not not_424 (not_424_out, F0);
  not not_425 (not_425_out, OP5);
  not not_426 (not_426_out, OP4);
  not not_427 (not_427_out, OP3);
  not not_428 (not_428_out, OP2);
  not not_429 (not_429_out, OP1);
  not not_430 (not_430_out, OP0);
  not not_431 (not_431_out, F4);
  not not_432 (not_432_out, F3);
  not not_433 (not_433_out, F1);
  not not_434 (not_434_out, OP5);
  not not_435 (not_435_out, OP4);
  not not_436 (not_436_out, OP3);
  not not_437 (not_437_out, OP2);
  not not_438 (not_438_out, OP1);
  not not_439 (not_439_out, OP0);
  not not_440 (not_440_out, F4);
  not not_441 (not_441_out, F3);
  not not_442 (not_442_out, OP5);
  not not_443 (not_443_out, OP4);
  not not_444 (not_444_out, OP3);
  not not_445 (not_445_out, OP2);
  not not_446 (not_446_out, OP1);
  not not_447 (not_447_out, OP0);
  not not_448 (not_448_out, F4);
  not not_449 (not_449_out, F2);
  not not_450 (not_450_out, F0);
  not not_451 (not_451_out, OP5);
  not not_452 (not_452_out, OP4);
  not not_453 (not_453_out, OP3);
  not not_454 (not_454_out, OP2);
  not not_455 (not_455_out, OP1);
  not not_456 (not_456_out, OP0);
  not not_457 (not_457_out, F4);
  not not_458 (not_458_out, F2);
  not not_459 (not_459_out, OP5);
  not not_460 (not_460_out, OP4);
  not not_461 (not_461_out, OP3);
  not not_462 (not_462_out, OP2);
  not not_463 (not_463_out, OP1);
  not not_464 (not_464_out, OP0);
  not not_465 (not_465_out, F5);
  not not_466 (not_466_out, F4);
  not not_467 (not_467_out, F2);
  not not_468 (not_468_out, F1);
  not not_469 (not_469_out, F0);
  not not_470 (not_470_out, OP5);
  not not_471 (not_471_out, OP4);
  not not_472 (not_472_out, OP3);
  not not_473 (not_473_out, OP2);
  not not_474 (not_474_out, OP1);
  not not_475 (not_475_out, OP0);
  not not_476 (not_476_out, F5);
  not not_477 (not_477_out, F4);
  not not_478 (not_478_out, F1);
  not not_479 (not_479_out, F0);
  not not_480 (not_480_out, OP5);
  not not_481 (not_481_out, OP4);
  not not_482 (not_482_out, OP3);
  not not_483 (not_483_out, OP1);
  not not_484 (not_484_out, OP0);
  not not_485 (not_485_out, OP5);
  not not_486 (not_486_out, OP4);
  not not_487 (not_487_out, OP3);
  not not_488 (not_488_out, OP1);
  not not_489 (not_489_out, OP5);
  not not_490 (not_490_out, OP4);
  not not_491 (not_491_out, OP2);
  not not_492 (not_492_out, OP1);
  not not_493 (not_493_out, OP0);
  not not_494 (not_494_out, OP5);
  not not_495 (not_495_out, OP4);
  not not_496 (not_496_out, OP1);
  not not_497 (not_497_out, OP0);
  not not_498 (not_498_out, OP5);
  not not_499 (not_499_out, OP4);
  not not_500 (not_500_out, OP2);
  not not_501 (not_501_out, OP1);
  not not_502 (not_502_out, OP5);
  not not_503 (not_503_out, OP4);
  not not_504 (not_504_out, OP2);
  not not_505 (not_505_out, OP0);
  not not_506 (not_506_out, OP5);
  not not_507 (not_507_out, OP4);
  not not_508 (not_508_out, OP1);
  not not_509 (not_509_out, OP4);
  not not_510 (not_510_out, OP3);
  not not_511 (not_511_out, OP2);
  not not_512 (not_512_out, OP4);
  not not_513 (not_513_out, OP2);
  not not_514 (not_514_out, OP5);
  not not_515 (not_515_out, OP4);
  not not_516 (not_516_out, OP3);
  not not_517 (not_517_out, OP2);
  not not_518 (not_518_out, OP1);
  not not_519 (not_519_out, OP0);
  not not_520 (not_520_out, F5);
  not not_521 (not_521_out, F4);
  not not_522 (not_522_out, F3);
  not not_523 (not_523_out, F0);
  not not_524 (not_524_out, OP5);
  not not_525 (not_525_out, OP4);
  not not_526 (not_526_out, OP0);
  not not_527 (not_527_out, OP4);
  not not_528 (not_528_out, OP2);
  not not_529 (not_529_out, OP1);
  not not_530 (not_530_out, OP0);
  not not_531 (not_531_out, OP5);
  not not_532 (not_532_out, OP4);
  not not_533 (not_533_out, OP3);
  not not_534 (not_534_out, OP2);
  not not_535 (not_535_out, OP1);
  not not_536 (not_536_out, OP5);
  not not_537 (not_537_out, OP4);
  not not_538 (not_538_out, OP3);
  not not_539 (not_539_out, OP2);
  not not_540 (not_540_out, OP1);
  not not_541 (not_541_out, OP0);
  not not_542 (not_542_out, F5);
  not not_543 (not_543_out, F4);
  not not_544 (not_544_out, F3);
  not not_545 (not_545_out, F2);
  not not_546 (not_546_out, F1);
  not not_547 (not_547_out, F0);
  not not_548 (not_548_out, OP5);
  not not_549 (not_549_out, OP4);
  not not_550 (not_550_out, OP3);
  not not_551 (not_551_out, OP2);
  not not_552 (not_552_out, OP1);
  not not_553 (not_553_out, OP0);
  not not_554 (not_554_out, F5);
  not not_555 (not_555_out, F4);
  not not_556 (not_556_out, F3);
  not not_557 (not_557_out, F2);
  not not_558 (not_558_out, OP5);
  not not_559 (not_559_out, OP4);
  not not_560 (not_560_out, OP3);
  not not_561 (not_561_out, OP2);
  not not_562 (not_562_out, OP1);
  not not_563 (not_563_out, OP0);
  not not_564 (not_564_out, F5);
  not not_565 (not_565_out, F4);
  not not_566 (not_566_out, F3);
  not not_567 (not_567_out, F2);
  not not_568 (not_568_out, F0);
  not not_569 (not_569_out, OP5);
  not not_570 (not_570_out, OP4);
  not not_571 (not_571_out, OP3);
  not not_572 (not_572_out, OP2);
  not not_573 (not_573_out, OP1);
  not not_574 (not_574_out, OP0);
  not not_575 (not_575_out, F4);
  not not_576 (not_576_out, F3);
  not not_577 (not_577_out, F2);
  not not_578 (not_578_out, F1);
  not not_579 (not_579_out, F0);
  not not_580 (not_580_out, OP5);
  not not_581 (not_581_out, OP4);
  not not_582 (not_582_out, OP3);
  not not_583 (not_583_out, OP2);
  not not_584 (not_584_out, OP1);
  not not_585 (not_585_out, OP0);
  not not_586 (not_586_out, F4);
  not not_587 (not_587_out, F3);
  not not_588 (not_588_out, F2);
  not not_589 (not_589_out, F1);
  not not_590 (not_590_out, OP5);
  not not_591 (not_591_out, OP4);
  not not_592 (not_592_out, OP3);
  not not_593 (not_593_out, OP2);
  not not_594 (not_594_out, OP1);
  not not_595 (not_595_out, OP0);
  not not_596 (not_596_out, F4);
  not not_597 (not_597_out, F3);
  not not_598 (not_598_out, F2);
  not not_599 (not_599_out, F0);
  not not_600 (not_600_out, OP5);
  not not_601 (not_601_out, OP4);
  not not_602 (not_602_out, OP3);
  not not_603 (not_603_out, OP2);
  not not_604 (not_604_out, OP1);
  not not_605 (not_605_out, OP0);
  not not_606 (not_606_out, F4);
  not not_607 (not_607_out, F3);
  not not_608 (not_608_out, F1);
  not not_609 (not_609_out, F0);
  not not_610 (not_610_out, OP5);
  not not_611 (not_611_out, OP4);
  not not_612 (not_612_out, OP3);
  not not_613 (not_613_out, OP2);
  not not_614 (not_614_out, OP1);
  not not_615 (not_615_out, OP0);
  not not_616 (not_616_out, F4);
  not not_617 (not_617_out, F3);
  not not_618 (not_618_out, F1);
  not not_619 (not_619_out, OP5);
  not not_620 (not_620_out, OP4);
  not not_621 (not_621_out, OP3);
  not not_622 (not_622_out, OP2);
  not not_623 (not_623_out, OP1);
  not not_624 (not_624_out, OP0);
  not not_625 (not_625_out, F4);
  not not_626 (not_626_out, F3);
  not not_627 (not_627_out, OP5);
  not not_628 (not_628_out, OP4);
  not not_629 (not_629_out, OP3);
  not not_630 (not_630_out, OP2);
  not not_631 (not_631_out, OP1);
  not not_632 (not_632_out, OP0);
  not not_633 (not_633_out, F4);
  not not_634 (not_634_out, F2);
  not not_635 (not_635_out, F0);
  not not_636 (not_636_out, OP5);
  not not_637 (not_637_out, OP4);
  not not_638 (not_638_out, OP3);
  not not_639 (not_639_out, OP2);
  not not_640 (not_640_out, OP1);
  not not_641 (not_641_out, OP0);
  not not_642 (not_642_out, F4);
  not not_643 (not_643_out, F2);
  not not_644 (not_644_out, OP5);
  not not_645 (not_645_out, OP4);
  not not_646 (not_646_out, OP3);
  not not_647 (not_647_out, OP2);
  not not_648 (not_648_out, OP1);
  not not_649 (not_649_out, OP0);
  not not_650 (not_650_out, F5);
  not not_651 (not_651_out, F4);
  not not_652 (not_652_out, F1);
  not not_653 (not_653_out, F0);
  not not_654 (not_654_out, OP5);
  not not_655 (not_655_out, OP4);
  not not_656 (not_656_out, OP3);
  not not_657 (not_657_out, OP1);
  not not_658 (not_658_out, OP0);
  not not_659 (not_659_out, OP5);
  not not_660 (not_660_out, OP4);
  not not_661 (not_661_out, OP3);
  not not_662 (not_662_out, OP1);
  not not_663 (not_663_out, OP4);
  not not_664 (not_664_out, OP2);
  not not_665 (not_665_out, OP5);
  not not_666 (not_666_out, OP4);
  not not_667 (not_667_out, OP3);
  not not_668 (not_668_out, OP2);
  not not_669 (not_669_out, OP1);
  not not_670 (not_670_out, OP0);
  not not_671 (not_671_out, F5);
  not not_672 (not_672_out, F4);
  not not_673 (not_673_out, F3);
  not not_674 (not_674_out, F0);
  not not_675 (not_675_out, OP4);
  not not_676 (not_676_out, OP2);
  not not_677 (not_677_out, OP1);
  not not_678 (not_678_out, OP0);
  and and_1 (MemToReg, OP5, not_1_out, not_2_out, not_3_out, OP1, OP0);
  and and_2 (and_2_out, not_4_out, not_5_out, not_6_out, OP3, not_7_out, OP5);
  and and_3 (and_3_out, OP0, OP1, not_8_out, OP3, not_9_out, OP5);
  and and_4 (and_4_out, not_10_out, not_11_out, OP3, not_12_out, not_13_out, not_14_out);
  and and_5 (and_5_out, not_15_out, not_16_out, OP3, OP2, not_17_out, not_18_out);
  and and_6 (and_6_out, not_19_out, not_20_out, OP3, not_21_out, not_22_out, OP0);
  and and_7 (and_7_out, not_23_out, not_24_out, OP3, not_25_out, OP1, not_26_out);
  and and_8 (and_8_out, not_27_out, not_28_out, OP3, OP2, not_29_out, OP0);
  and and_9 (and_9_out, OP5, not_30_out, not_31_out, not_32_out, OP1, OP0);
  and and_10 (and_10_out, OP5, not_33_out, OP3, not_34_out, OP1, OP0);
  and and_11 (and_11_out, not_35_out, not_36_out, OP3, OP2, OP1, not_37_out);
  and and_12 (and_12_out, OP5, not_38_out, OP3, not_39_out, not_40_out, not_41_out);
  and and_13 (and_13_out, not_42_out, not_43_out, not_44_out, not_45_out, not_46_out, not_47_out, not_48_out, not_49_out, not_50_out, not_51_out, not_52_out, not_53_out);
  and and_14 (and_14_out, not_54_out, not_55_out, not_56_out, not_57_out, not_58_out, not_59_out, not_60_out, not_61_out, not_62_out, not_63_out, F1, F0);
  and and_15 (and_15_out, not_64_out, not_65_out, not_66_out, not_67_out, not_68_out, not_69_out, not_70_out, not_71_out, not_72_out, not_73_out, F1, not_74_out);
  and and_16 (and_16_out, not_75_out, not_76_out, not_77_out, not_78_out, not_79_out, not_80_out, F5, not_81_out, not_82_out, not_83_out, not_84_out, not_85_out);
  and and_17 (and_17_out, not_86_out, not_87_out, not_88_out, not_89_out, not_90_out, not_91_out, F5, not_92_out, not_93_out, not_94_out, not_95_out, F0);
  and and_18 (and_18_out, not_96_out, not_97_out, not_98_out, not_99_out, not_100_out, not_101_out, F5, not_102_out, not_103_out, not_104_out, F1, not_105_out);
  and and_19 (and_19_out, not_106_out, not_107_out, not_108_out, not_109_out, not_110_out, not_111_out, F5, not_112_out, not_113_out, F2, not_114_out, not_115_out);
  and and_20 (and_20_out, not_116_out, not_117_out, not_118_out, not_119_out, not_120_out, not_121_out, F5, not_122_out, not_123_out, F2, not_124_out, F0);
  and and_21 (and_21_out, not_125_out, not_126_out, not_127_out, not_128_out, not_129_out, not_130_out, F5, not_131_out, not_132_out, F2, F1, F0);
  and and_22 (and_22_out, not_133_out, not_134_out, not_135_out, not_136_out, not_137_out, not_138_out, F5, not_139_out, F3, not_140_out, F1, not_141_out);
  and and_23 (and_23_out, not_142_out, not_143_out, not_144_out, not_145_out, not_146_out, not_147_out, F5, not_148_out, F3, not_149_out, F1, F0);
  and and_24 (and_24_out, not_150_out, not_151_out, not_152_out, not_153_out, OP1, OP0);
  and and_25 (and_25_out, not_154_out, not_155_out, OP3, not_156_out, not_157_out, not_158_out);
  and and_26 (and_26_out, not_159_out, not_160_out, OP3, OP2, not_161_out, not_162_out);
  and and_27 (and_27_out, not_163_out, not_164_out, OP3, not_165_out, not_166_out, OP0);
  and and_28 (and_28_out, not_167_out, not_168_out, OP3, not_169_out, OP1, not_170_out);
  and and_29 (and_29_out, not_171_out, not_172_out, OP3, OP2, not_173_out, OP0);
  and and_30 (and_30_out, OP5, not_174_out, not_175_out, not_176_out, OP1, OP0);
  and and_31 (and_31_out, not_177_out, not_178_out, not_179_out, not_180_out, not_181_out, not_182_out, not_183_out, not_184_out, not_185_out, F2, F1, not_186_out);
  and and_32 (and_32_out, not_187_out, not_188_out, OP3, OP2, OP1, not_189_out);
  and and_33 (SysCALL, not_190_out, not_191_out, not_192_out, not_193_out, not_194_out, not_195_out, not_196_out, not_197_out, F3, F2, not_198_out, not_199_out);
  and and_34 (and_34_out, not_200_out, not_201_out, OP3, not_202_out, not_203_out, not_204_out);
  and and_35 (and_35_out, not_205_out, not_206_out, OP3, not_207_out, not_208_out, OP0);
  and and_36 (and_36_out, not_209_out, not_210_out, OP3, not_211_out, OP1, not_212_out);
  and and_37 (and_37_out, OP5, not_213_out, not_214_out, not_215_out, OP1, OP0);
  and and_38 (and_38_out, OP5, not_216_out, OP3, not_217_out, OP1, OP0);
  and and_39 (and_39_out, OP5, not_218_out, OP3, not_219_out, not_220_out, not_221_out);
  and and_40 (and_40_out, not_222_out, not_223_out, not_224_out, not_225_out, not_226_out, not_227_out, not_228_out, not_229_out, not_230_out, not_231_out, not_232_out, not_233_out);
  and and_41 (and_41_out, not_234_out, not_235_out, not_236_out, not_237_out, not_238_out, not_239_out, not_240_out, not_241_out, not_242_out, not_243_out, F1, F0);
  and and_42 (and_42_out, not_244_out, not_245_out, not_246_out, not_247_out, not_248_out, not_249_out, not_250_out, not_251_out, not_252_out, not_253_out, F1, not_254_out);
  and and_43 (and_43_out, not_255_out, not_256_out, not_257_out, not_258_out, not_259_out, not_260_out, F5, not_261_out, not_262_out, not_263_out, not_264_out, not_265_out);
  and and_44 (and_44_out, not_266_out, not_267_out, not_268_out, not_269_out, not_270_out, not_271_out, F5, not_272_out, not_273_out, not_274_out, not_275_out, F0);
  and and_45 (and_45_out, not_276_out, not_277_out, not_278_out, not_279_out, not_280_out, not_281_out, F5, not_282_out, not_283_out, not_284_out, F1, not_285_out);
  and and_46 (and_46_out, not_286_out, not_287_out, not_288_out, not_289_out, not_290_out, not_291_out, F5, not_292_out, not_293_out, F2, not_294_out, not_295_out);
  and and_47 (and_47_out, not_296_out, not_297_out, not_298_out, not_299_out, not_300_out, not_301_out, F5, not_302_out, not_303_out, F2, not_304_out, F0);
  and and_48 (and_48_out, not_305_out, not_306_out, not_307_out, not_308_out, not_309_out, not_310_out, F5, not_311_out, not_312_out, F2, F1, F0);
  and and_49 (and_49_out, not_313_out, not_314_out, not_315_out, not_316_out, not_317_out, not_318_out, F5, not_319_out, F3, not_320_out, F1, not_321_out);
  and and_50 (and_50_out, not_322_out, not_323_out, not_324_out, not_325_out, not_326_out, not_327_out, F5, not_328_out, F3, not_329_out, F1, F0);
  and and_51 (and_51_out, not_330_out, not_331_out, not_332_out, not_333_out, not_334_out, not_335_out, not_336_out, not_337_out, not_338_out, F2, F1, not_339_out);
  and and_52 (and_52_out, not_340_out, not_341_out, OP3, OP2, OP1, not_342_out);
  and and_53 (BEQ, not_343_out, not_344_out, not_345_out, OP2, not_346_out, not_347_out);
  and and_54 (BNE, not_348_out, not_349_out, not_350_out, OP2, not_351_out, OP0);
  and and_55 (JR, not_352_out, not_353_out, not_354_out, not_355_out, not_356_out, not_357_out, not_358_out, not_359_out, F3, not_360_out, not_361_out, not_362_out);
  and and_56 (JUMP, not_363_out, not_364_out, not_365_out, not_366_out, OP1, not_367_out);
  and and_57 (JAL, not_368_out, not_369_out, not_370_out, not_371_out, OP1, OP0);
  and and_58 (RS_SHAMT, not_372_out, not_373_out, OP3, OP2, OP1, not_374_out);
  and and_59 (SB, OP5, not_375_out, OP3, not_376_out, not_377_out, not_378_out);
  and and_60 (BLTZ, not_379_out, not_380_out, not_381_out, not_382_out, not_383_out, OP0);
  and and_61 (and_61_out, not_384_out, not_385_out, not_386_out, not_387_out, not_388_out, not_389_out, F5, not_390_out, not_391_out, not_392_out, not_393_out, not_394_out);
  and and_62 (and_62_out, not_395_out, not_396_out, not_397_out, not_398_out, not_399_out, not_400_out, F5, not_401_out, not_402_out, not_403_out, not_404_out, F0);
  and and_63 (and_63_out, not_405_out, not_406_out, not_407_out, not_408_out, not_409_out, not_410_out, F5, not_411_out, not_412_out, not_413_out, F1, not_414_out);
  and and_64 (and_64_out, not_415_out, not_416_out, not_417_out, not_418_out, not_419_out, not_420_out, F5, not_421_out, not_422_out, F2, not_423_out, not_424_out);
  and and_65 (and_65_out, not_425_out, not_426_out, not_427_out, not_428_out, not_429_out, not_430_out, F5, not_431_out, not_432_out, F2, not_433_out, F0);
  and and_66 (and_66_out, not_434_out, not_435_out, not_436_out, not_437_out, not_438_out, not_439_out, F5, not_440_out, not_441_out, F2, F1, F0);
  and and_67 (and_67_out, not_442_out, not_443_out, not_444_out, not_445_out, not_446_out, not_447_out, F5, not_448_out, F3, not_449_out, F1, not_450_out);
  and and_68 (and_68_out, not_451_out, not_452_out, not_453_out, not_454_out, not_455_out, not_456_out, F5, not_457_out, F3, not_458_out, F1, F0);
  and and_69 (and_69_out, not_459_out, not_460_out, not_461_out, not_462_out, not_463_out, not_464_out, not_465_out, not_466_out, F3, not_467_out, not_468_out, not_469_out);
  and and_70 (and_70_out, not_470_out, not_471_out, not_472_out, not_473_out, not_474_out, not_475_out, not_476_out, not_477_out, F3, F2, not_478_out, not_479_out);
  and and_71 (and_71_out, not_480_out, not_481_out, not_482_out, OP2, not_483_out, not_484_out);
  and and_72 (and_72_out, not_485_out, not_486_out, not_487_out, OP2, not_488_out, OP0);
  and and_73 (and_73_out, not_489_out, not_490_out, OP3, not_491_out, not_492_out, not_493_out);
  and and_74 (and_74_out, not_494_out, not_495_out, OP3, OP2, not_496_out, not_497_out);
  and and_75 (and_75_out, not_498_out, not_499_out, OP3, not_500_out, not_501_out, OP0);
  and and_76 (and_76_out, not_502_out, not_503_out, OP3, not_504_out, OP1, not_505_out);
  and and_77 (and_77_out, not_506_out, not_507_out, OP3, OP2, not_508_out, OP0);
  and and_78 (and_78_out, OP5, not_509_out, not_510_out, not_511_out, OP1, OP0);
  and and_79 (and_79_out, OP5, not_512_out, OP3, not_513_out, OP1, OP0);
  and and_80 (and_80_out, not_514_out, not_515_out, not_516_out, not_517_out, not_518_out, not_519_out, not_520_out, not_521_out, not_522_out, F2, F1, not_523_out);
  and and_81 (and_81_out, not_524_out, not_525_out, OP3, OP2, OP1, not_526_out);
  and and_82 (and_82_out, OP5, not_527_out, OP3, not_528_out, not_529_out, not_530_out);
  and and_83 (and_83_out, not_531_out, not_532_out, not_533_out, not_534_out, not_535_out, OP0);
  and and_84 (and_84_out, not_536_out, not_537_out, not_538_out, not_539_out, not_540_out, not_541_out, not_542_out, not_543_out, not_544_out, not_545_out, not_546_out, not_547_out);
  and and_85 (and_85_out, not_548_out, not_549_out, not_550_out, not_551_out, not_552_out, not_553_out, not_554_out, not_555_out, not_556_out, not_557_out, F1, F0);
  and and_86 (and_86_out, not_558_out, not_559_out, not_560_out, not_561_out, not_562_out, not_563_out, not_564_out, not_565_out, not_566_out, not_567_out, F1, not_568_out);
  and and_87 (and_87_out, not_569_out, not_570_out, not_571_out, not_572_out, not_573_out, not_574_out, F5, not_575_out, not_576_out, not_577_out, not_578_out, not_579_out);
  and and_88 (and_88_out, not_580_out, not_581_out, not_582_out, not_583_out, not_584_out, not_585_out, F5, not_586_out, not_587_out, not_588_out, not_589_out, F0);
  and and_89 (and_89_out, not_590_out, not_591_out, not_592_out, not_593_out, not_594_out, not_595_out, F5, not_596_out, not_597_out, not_598_out, F1, not_599_out);
  and and_90 (and_90_out, not_600_out, not_601_out, not_602_out, not_603_out, not_604_out, not_605_out, F5, not_606_out, not_607_out, F2, not_608_out, not_609_out);
  and and_91 (and_91_out, not_610_out, not_611_out, not_612_out, not_613_out, not_614_out, not_615_out, F5, not_616_out, not_617_out, F2, not_618_out, F0);
  and and_92 (and_92_out, not_619_out, not_620_out, not_621_out, not_622_out, not_623_out, not_624_out, F5, not_625_out, not_626_out, F2, F1, F0);
  and and_93 (and_93_out, not_627_out, not_628_out, not_629_out, not_630_out, not_631_out, not_632_out, F5, not_633_out, F3, not_634_out, F1, not_635_out);
  and and_94 (and_94_out, not_636_out, not_637_out, not_638_out, not_639_out, not_640_out, not_641_out, F5, not_642_out, F3, not_643_out, F1, F0);
  and and_95 (and_95_out, not_644_out, not_645_out, not_646_out, not_647_out, not_648_out, not_649_out, not_650_out, not_651_out, F3, F2, not_652_out, not_653_out);
  and and_96 (and_96_out, not_654_out, not_655_out, not_656_out, OP2, not_657_out, not_658_out);
  and and_97 (and_97_out, not_659_out, not_660_out, not_661_out, OP2, not_662_out, OP0);
  and and_98 (and_98_out, OP5, not_663_out, OP3, not_664_out, OP1, OP0);
  and and_99 (and_99_out, not_665_out, not_666_out, not_667_out, not_668_out, not_669_out, not_670_out, not_671_out, not_672_out, not_673_out, F2, F1, not_674_out);
  and and_100 (and_100_out, OP5, not_675_out, OP3, not_676_out, not_677_out, not_678_out);
  or or_1 (MemWrite, and_2_out, and_3_out);
  or or_2 (ALU_SRC, and_4_out, and_5_out, and_6_out, and_7_out, and_8_out, and_9_out, and_10_out, and_11_out, and_12_out);
  or or_3 (SignedExt, and_34_out, and_35_out, and_36_out, and_37_out, and_38_out, and_39_out);
  or or_4 (RegWrite, and_13_out, and_14_out, and_15_out, and_16_out, and_17_out, and_18_out, and_19_out, and_20_out, and_21_out, and_22_out, and_23_out, and_24_out, and_25_out, and_26_out, and_27_out, and_28_out, and_29_out, and_30_out, and_31_out, and_32_out);
  or or_5 (RegDst, and_40_out, and_41_out, and_42_out, and_43_out, and_44_out, and_45_out, and_46_out, and_47_out, and_48_out, and_49_out, and_50_out, and_51_out, and_52_out);
  or or_6 (R1_Used, and_61_out, and_62_out, and_63_out, and_64_out, and_65_out, and_66_out, and_67_out, and_68_out, and_69_out, and_70_out, and_71_out, and_72_out, and_73_out, and_74_out, and_75_out, and_76_out, and_77_out, and_78_out, and_79_out, and_80_out, and_81_out, and_82_out, and_83_out);
  or or_7 (R2_Used, and_84_out, and_85_out, and_86_out, and_87_out, and_88_out, and_89_out, and_90_out, and_91_out, and_92_out, and_93_out, and_94_out, and_95_out, and_96_out, and_97_out, and_98_out, and_99_out, and_100_out);
endmodule

// ALU
module MIPS_ALU (
  input  [4:0] shamt,
  input  [31:0] X,
  input  [31:0] Y,
  input  [3:0] AluOP,
  output Equal,
  output [31:0] Result,
  output [31:0] Result_2
);

  wire [0:0] comparator_1_lt, comparator_2_lt;
  wire [31:0] adder_1_out, AND_out, divider_1_out, divider_1_rem, multiplier_1_cout, multiplier_1_out,
       NOR_out, OR_out, shifter_1_out, shifter_2_out, shifter_3_out, subtractor_1_out, XOR_out;

  assign AND_out = X & Y;  // AND_Gate AND, 32 bits wide
  assign OR_out = X | Y;  // OR_Gate OR, 32 bits wide
  Shifter #(.width(32), .shift("ll")) shifter_1 (.in(Y), .\dist (shamt), .out(shifter_1_out));
  Shifter #(.width(32), .shift("ar")) shifter_2 (.in(Y), .\dist (shamt), .out(shifter_2_out));
  Shifter #(.width(32), .shift("lr")) shifter_3 (.in(Y), .\dist (shamt), .out(shifter_3_out));
  Multiplier #(.width(32)) multiplier_1 (.a(X), .b(Y), .out(multiplier_1_out), .cout(multiplier_1_cout));  // open: cin
  Divider #(.width(32)) divider_1 (.a(X), .b(Y), .out(divider_1_out), .rem(divider_1_rem));  // open: upper
  Adder #(.width(32)) adder_1 (.a(X), .b(Y), .out(adder_1_out));  // open: cin, cout
  Subtractor #(.width(32)) subtractor_1 (.a(X), .b(Y), .out(subtractor_1_out));  // open: bin, bout
  assign XOR_out = X ^ Y;  // XOR_Gate XOR, 32 bits wide
  assign NOR_out = ~(X | Y);  // NOR_Gate NOR, 32 bits wide
  Comparator #(.width(32), .mode("twosComplement")) comparator_1 (
    .a(X), .b(Y), .eq(Equal), .lt(comparator_1_lt[0]));  // open: gt
  Comparator #(.width(32), .mode("unsigned")) comparator_2 (.a(X), .b(Y), .lt(comparator_2_lt[0]));  // open: gt, eq
  Multiplexer #(.select(4), .width(32), .disabled("Z"), .enable("false")) multiplexer_1 (
    .in0(shifter_1_out), .in1(shifter_2_out), .in2(shifter_3_out), .in3(multiplier_1_out),
    .in4(divider_1_out), .in5(adder_1_out), .in6(subtractor_1_out), .in7(AND_out), .in8(OR_out),
    .in9(XOR_out), .in10(NOR_out), .in11({{31{1'b0}}, comparator_1_lt[0]}),
    .in12({{31{1'b0}}, comparator_2_lt[0]}), .in13({32{1'b0}}), .in14({32{1'b0}}), .in15({32{1'b0}}),
    .out(Result), .sel(AluOP));
  Multiplexer #(.select(4), .width(32), .disabled("Z"), .enable("false")) multiplexer_2 (
    .in0({32{1'b0}}), .in1({32{1'b0}}), .in2({32{1'b0}}), .in3(multiplier_1_cout), .in4(divider_1_rem),
    .in5({32{1'b0}}), .in6({32{1'b0}}), .in7({32{1'b0}}), .in8({32{1'b0}}), .in9({32{1'b0}}),
    .in10({32{1'b0}}), .in11({32{1'b0}}), .in12({32{1'b0}}), .in13({32{1'b0}}), .in14({32{1'b0}}),
    .in15({32{1'b0}}), .out(Result_2), .sel(AluOP));

  // Other names for the same wires on the sheet: Result2[31:0] = Result_2; S[3:0] = AluOP

  // Notes on the sheet:
  //   不要改变此引脚区域内容，也不要改变ALU封装形式
  //   输入引脚
  //   输出引脚
endmodule

module MIPS_Regifile (
  input  [31:0] Din,
  input  Clk,
  input  WE,
  input  [4:0] R1_num,
  input  [4:0] W_num,
  input  [4:0] R2_num,
  output [31:0] R1,
  output [31:0] R2
);

  // RegisterFile registerfile_1: pin names not known; wires that end beside it: Din, Clk, WE, W_num, R1_num, R2_num, R1, R2
endmodule

module \理想流水线  (
);

  wire and_1_out, and_2_out, and_3_out, CLK, comparator_1_eq, ex_mem_1_p13, ex_mem_1_p14, ex_mem_1_p15,
       ex_mem_1_p16, ex_mem_1_p17, ex_mem_1_p20, ex_mem_1_p21, EXBranch, Go, id_ex_1_p1, id_ex_1_p8,
       id_ex_1_p10, id_ex_1_p11, id_ex_1_p12, id_ex_1_p13, id_ex_1_p14, id_ex_1_p15, id_ex_1_p16,
       id_ex_1_p17, id_ex_1_p18, id_ex_1_p19, id_ex_1_p20, id_ex_1_p21, IDBranch, IR1, IR2, IR3, JAL,
       mem_wb_1_p11, mips_alu_1_p5, mips_alu_1_p6, mips_alu_1_p8, not_1_out, or_2_out, or_3_out, RegDst,
       RegWrite, Running, Syscall, W1, W2, W3, \单周期硬布线控制器_1_p1 , \单周期硬布线控制器_1_p2 ;
  wire [4:0] multiplexer_4_out, multiplexer_5_out, multiplexer_6_out, multiplexer_7_out;
  wire [11:0] EX_PC, ID_PC, IF_PC, MEM_PC, WB_PC;
  wire [15:0] id_ex_1_p23, if_id_1_out_6, \LoadUse次数 , \总周期数 , \插入气泡数 , \无条件分支数 , \条件分支成功数 ;
  wire [27:0] if_id_1_out_7;
  wire [31:0] adder_1_out, adder_2_out, bit_extender_1_out, bit_extender_2_out, ex_mem_1_p18, ex_mem_1_p19,
       id_ex_1_p22, id_ex_1_p24, id_ex_1_p25, LedData, mem_wb_1_p15, mem_wb_1_p16, mem_wb_1_p17,
       mem_wb_1_p18, mips_alu_1_p2, multiplexer_1_out, multiplexer_2_out, multiplexer_3_out,
       multiplexer_8_out, multiplexer_9_out, multiplexer_11_out, PC_q, R1, R2, ram_1_data, rom_1_data,
       shifter_1_out;
  wire [31:18] if_id_1_out_6_2;
  wire [31:26] if_id_1_out_6_3;

  Button \u_总复位  (.out(Go));
  Button _1 (.out(IR1));
  Button _2 (.out(IR2));
  Button _3 (.out(IR3));
  Button \u_继续运行  (.out(Go));
  LED #(.active("true")) led_1 (.in(W1));
  LED #(.active("true")) led_2 (.in(W2));
  LED #(.active("true")) led_3 (.in(W3));
  Hex_Digit_Display hex_digit_display_1 (.value(LedData[31:28]));  // open: dp
  Hex_Digit_Display hex_digit_display_2 (.value(LedData[23:20]));  // open: dp
  Hex_Digit_Display hex_digit_display_3 (.value(LedData[27:24]));  // open: dp
  Multiplexer #(.select(1), .width(32), .disabled("Z"), .enable("false")) multiplexer_1 (
    .in0(adder_1_out), .in1(R1), .out(multiplexer_1_out), .sel(\单周期硬布线控制器_1_p2 ));
  Multiplexer #(.select(1), .width(32), .disabled("Z"), .enable("false")) multiplexer_2 (
    .in0(multiplexer_1_out), .in1({if_id_1_out_6_2, if_id_1_out_6, 2'b00}), .out(multiplexer_2_out),
    .sel(or_2_out));
  Hex_Digit_Display hex_digit_display_4 (.value(LedData[15:12]));  // open: dp
  Hex_Digit_Display hex_digit_display_5 (.value(LedData[19:16]));  // open: dp
  Register #(.width(32), .trigger("rising"), .Select("low")) PC (
    .D(multiplexer_3_out), .en(Running), .Q(PC_q), .clk(CLK), .clr(Go));
  Multiplexer #(.select(1), .width(32), .disabled("Z"), .enable("false")) multiplexer_3 (
    .in0(multiplexer_2_out), .in1(adder_2_out), .out(multiplexer_3_out), .sel(EXBranch));
  Hex_Digit_Display hex_digit_display_6 (.value(LedData[11:8]));  // open: dp
  Hex_Digit_Display hex_digit_display_7 (.value(LedData[7:4]));  // open: dp
  Clock #(.highDuration(1), .lowDuration(1)) clock_1 (.out(CLK));
  Hex_Digit_Display hex_digit_display_8 (.value(LedData[3:0]));  // open: dp
  or or_1 (IDBranch, \单周期硬布线控制器_1_p2 , or_2_out);
  Adder #(.width(32)) adder_1 (.a(PC_q), .b(32'h4), .out(adder_1_out));  // open: cin, cout
  buf or_2 (or_2_out, \单周期硬布线控制器_1_p1 );  // OR_Gate
  // Probe on rom_1_data
  ROM #(.addrWidth(10), .dataWidth(32), .Select("high")) rom_1 (.addr(PC_q[11:2]), .data(rom_1_data));
  // Probe on \总周期数 
  // Probe on \无条件分支数 
  // Probe on \条件分支成功数 
  // Probe on \插入气泡数 
  // Probe on \LoadUse次数 
  IF_ID if_id_1 (
    .in_1(CLK), .in_3(or_3_out), .in_4(rom_1_data), .in_5(adder_1_out),
    .out_6({if_id_1_out_6_3, if_id_1_out_6_2[27:18], if_id_1_out_6}),
    .out_7({if_id_1_out_6_2[31:28], if_id_1_out_7}));  // open: in_2
  or or_3 (or_3_out, Go, IDBranch, EXBranch);
  // Probe on IF_PC
  // Probe on {if_id_1_out_6_3, if_id_1_out_6_2[27:18], if_id_1_out_6}
  // Probe on if_id_1_out_6_3
  // Probe on {if_id_1_out_6_3, if_id_1_out_6_2[27:18], if_id_1_out_6}
  // Probe on EX_PC
  // Probe on ID_PC
  // 单周期硬布线控制器 单周期硬布线控制器_1: pin names not known; wires that end beside it: \单周期硬布线控制器_1_p1 , \单周期硬布线控制器_1_p2 , if_id_1_out_6_3, if_id_1_out_6[5:0], Syscall
  Multiplexer #(.select(1), .width(5), .disabled("Z"), .enable("false")) multiplexer_4 (
    .in0(if_id_1_out_6_2[27:23]), .in1(5'b00010), .out(multiplexer_4_out), .sel(Syscall));
  Multiplexer #(.select(1), .width(5), .disabled("Z"), .enable("false")) multiplexer_5 (
    .in0(if_id_1_out_6_2[22:18]), .in1(5'b00100), .out(multiplexer_5_out), .sel(Syscall));
  Multiplexer #(.select(1), .width(5), .disabled("Z"), .enable("false")) multiplexer_6 (
    .in0(mem_wb_1_p17[20:16]), .in1(mem_wb_1_p17[15:11]), .out(multiplexer_6_out), .sel(RegDst));
  // Probe on MEM_PC
  Multiplexer #(.select(1), .width(5), .disabled("Z"), .enable("false")) multiplexer_7 (
    .in0(multiplexer_6_out), .in1({5{1'b1}}), .out(multiplexer_7_out), .sel(JAL));
  Multiplexer #(.select(1), .width(32), .disabled("Z"), .enable("false")) multiplexer_8 (
    .in0(multiplexer_11_out), .in1(mem_wb_1_p18), .out(multiplexer_8_out), .sel(JAL));
  // Probe on WB_PC
  MIPS_Regifile mips_regifile_1 (
    .Din(multiplexer_8_out), .Clk(CLK), .R1(R1), .R2(R2), .WE(RegWrite), .W_num(multiplexer_7_out),
    .R1_num(multiplexer_4_out), .R2_num(multiplexer_5_out));
  // ID_EX id_ex_1: pin names not known; wires that end beside it: id_ex_1_p1, id_ex_1_p1, R1, R2, if_id_1_out_6, {if_id_1_out_6_3, if_id_1_out_6_2[27:18], if_id_1_out_6}, {if_id_1_out_6_2[31:28], if_id_1_out_7}, id_ex_1_p8, CLK, id_ex_1_p10, id_ex_1_p11, id_ex_1_p12, id_ex_1_p13, id_ex_1_p14, id_ex_1_p15, id_ex_1_p16, id_ex_1_p17, id_ex_1_p18, id_ex_1_p19, id_ex_1_p20, id_ex_1_p21, id_ex_1_p22, id_ex_1_p23, id_ex_1_p24, id_ex_1_p25
  or or_4 (id_ex_1_p10, Go, EXBranch);
  assign bit_extender_1_out = {{16{1'b0}}, id_ex_1_p23};  // Bit_Extender bit_extender_1
  assign bit_extender_2_out = {{16{id_ex_1_p23[15]}}, id_ex_1_p23};  // Bit_Extender bit_extender_2
  // Probe on id_ex_1_p24
  Multiplexer #(.select(1), .width(32), .disabled("Z"), .enable("false")) multiplexer_9 (
    .in0(bit_extender_1_out), .in1(bit_extender_2_out), .out(multiplexer_9_out), .sel(id_ex_1_p19));
  // Probe on bit_extender_2_out
  or or_5 (EXBranch, and_1_out, and_2_out);
  and and_1 (and_1_out, id_ex_1_p11, mips_alu_1_p5);
  // MIPS_ALU mips_alu_1: pin names not known; wires that end beside it: id_ex_1_p21, mips_alu_1_p2, id_ex_1_p15, id_ex_1_p24[10:6], mips_alu_1_p5, mips_alu_1_p6, id_ex_1_p20, mips_alu_1_p8
  Multiplexer #(.select(1), .width(32), .disabled("Z"), .enable("false")) multiplexer_10 (
    .in0(id_ex_1_p22), .in1(multiplexer_9_out), .out(mips_alu_1_p2), .sel(id_ex_1_p16));
  Shifter #(.width(32), .shift("ll")) shifter_1 (.in(bit_extender_2_out), .\dist (5'b00010), .out(shifter_1_out));
  and and_2 (and_2_out, id_ex_1_p12, ~mips_alu_1_p5);  // AND_Gate
  // EX_MEM ex_mem_1: pin names not known; wires that end beside it: id_ex_1_p13, id_ex_1_p14, id_ex_1_p17, id_ex_1_p18, id_ex_1_p20, mips_alu_1_p8, mips_alu_1_p6, id_ex_1_p22, id_ex_1_p24, id_ex_1_p25, CLK, Go, ex_mem_1_p13, ex_mem_1_p14, ex_mem_1_p15, ex_mem_1_p16, ex_mem_1_p17, ex_mem_1_p18, ex_mem_1_p19, ex_mem_1_p20, ex_mem_1_p21
  Adder #(.width(32)) adder_2 (.a(shifter_1_out), .b(id_ex_1_p25), .out(adder_2_out));  // open: cin, cout
  // Probe on ex_mem_1_p20
  RAM #(.addrWidth(10), .dataWidth(32), .bus("separate"), .Select("high")) ram_1 (
    .addr(ex_mem_1_p18[11:2]), .din(ex_mem_1_p19), .data(ram_1_data), .str(ex_mem_1_p14), .sel(Running),
    .clk(CLK), .clr(Go));  // open: ld
  // MEM_WB mem_wb_1: pin names not known; wires that end beside it: ex_mem_1_p13, ex_mem_1_p15, ex_mem_1_p16, ex_mem_1_p17, ex_mem_1_p18, ram_1_data, ex_mem_1_p20, ex_mem_1_p21, CLK, Go, mem_wb_1_p11, RegWrite, JAL, RegDst, mem_wb_1_p15, mem_wb_1_p16, mem_wb_1_p17, mem_wb_1_p18
  Multiplexer #(.select(1), .width(32), .disabled("Z"), .enable("false")) multiplexer_11 (
    .in0(mem_wb_1_p15), .in1(mem_wb_1_p16), .out(multiplexer_11_out), .sel(mem_wb_1_p11));
  // Probe on mem_wb_1_p17
  Comparator #(.width(32), .mode("twosComplement")) comparator_1 (
    .a(32'h22), .b(R1), .eq(comparator_1_eq));  // open: gt, lt
  and and_3 (and_3_out, comparator_1_eq, Syscall);
  not not_1 (not_1_out, comparator_1_eq);
  Register #(.width(32), .trigger("rising"), .Select("low")) register_1 (
    .D(R2), .en(and_3_out), .Q(LedData), .clk(CLK), .clr(Go));
  D_Flip_Flop #(.trigger("rising"), .Pre_Clr_Positions("ABOVE_BELOW"), .NegatePresetClear("false"), .enable("true"), .NewFFLayout("true")) d_ff_1 (
    .clk(CLK), .D(not_1_out), .Qn(Running), .en(Syscall), .reset(Go));  // open: Q, preset
  Counter #(.width(16), .max('hffff), .ongoal("wrap"), .trigger("rising"), .behavior("old")) \u_总周期数  (
    .count(Running), .Q(\总周期数 ), .carry(Go), .clk(CLK));  // open: load, D, clr, preset

  // Other names for the same wires on the sheet: RST = Go

  // Notes on the sheet:
  //   中断源
  //   中断等待指示
  //   数码管输出
  //   指令存储器
  //   contents of rom_1 (hex, n*v repeats v):
  //   20110100 20020022 8000006 20110004 20120005 20130006 10000003 20110007 20120008 20130009 14110003
  //   2011000a 2012000b 2013000c c000014 2002000a 0 0 0 c 2231ffff 0 0 0 112020 0 0 0 c 1620fff6 3e00008
  //   JMP
  //   JR
  //   OP
  //   OP
  //   Func
  //   Func
  //   rs
  //   rt
  //   rd
  //   Beq
  //   Bne
  //   AluOP
  //   AluSrcB
  //   RegWrite
  //   JAL
  //   BLTZ
  //   RegDst
  //   SignedExt
  //   SB
  //   Syscall
  //   流水调试日志用
  //   MemToReg
  //   MemWrite
  //   RS_SHAMT
endmodule
module \气泡流水线  (
);

  wire and_1_out, and_2_out, and_3_out, and_4_out, and_5_out, CLK, comparator_1_eq, dataCheck,
       ex_mem_1_out_18, ex_mem_1_out_19, ex_mem_1_out_24, ex_mem_1_out_25, ex_mem_1_out_26, ex_mem_1_out_27,
       EXRegWrite, Go, id_ex_1_out_29, id_ex_1_out_30, id_ex_1_out_31, id_ex_1_out_32, id_ex_1_out_34,
       id_ex_1_out_35, id_ex_1_out_37, id_ex_1_out_38, id_ex_1_out_39, id_ex_1_out_40, id_ex_1_out_41,
       id_ex_1_out_42, id_ex_1_out_43, IR1, IR2, IR3, JAL, JMP, JR, mem_wb_1_out_17, MEMRegWrite,
       mips_alu_1_equal, not_1_out, not_2_out, not_3_out, not_4_out, not_5_out, or_1_out, or_4_out, R1_Used,
       R2_Used, RegDst, RegWrite, Running, Syscall, W1, W2, W3, \单周期硬布线控制器_1_alu_src , \单周期硬布线控制器_1_beq ,
       \单周期硬布线控制器_1_bltz , \单周期硬布线控制器_1_bne , \单周期硬布线控制器_1_jal , \单周期硬布线控制器_1_jmp , \单周期硬布线控制器_1_jr ,
       \单周期硬布线控制器_1_memtoreg , \单周期硬布线控制器_1_memwrite , \单周期硬布线控制器_1_regdst , \单周期硬布线控制器_1_regwrite ,
       \单周期硬布线控制器_1_rs_shamt , \单周期硬布线控制器_1_sb , \单周期硬布线控制器_1_signedext , \单周期硬布线控制器_1_syscall , \无条件跳转 ,
       \有条件跳转 ;
  wire [3:0] id_ex_1_out_33, \单周期硬布线控制器_1_alu_op ;
  wire [4:0] A, B, EXWriteReg, id_ex_1_out_47, MEMWriteReg, multiplexer_6_out, multiplexer_7_out,
       multiplexer_12_out;
  wire [15:0] id_ex_1_out_49, if_id_1_out_6, \LoadUse次数 , \总周期数 , \插入气泡数 , \无条件分支数 , \条件分支成功数 ;
  wire [31:0] adder_1_out, adder_2_out, bit_extender_1_out, bit_extender_2_out, ex_mem_1_out_20,
       ex_mem_1_out_21, ex_mem_1_out_22, EX_PC, EXIR, id_ex_1_out_48, ID_PC, IF_PC, LedData, MEM_PC,
       mem_wb_1_out_15, mem_wb_1_out_20, mem_wb_1_out_21, MEMIR, mips_alu_1_result, mips_probe_1_p1,
       multiplexer_1_out, multiplexer_2_out, multiplexer_3_out, multiplexer_8_out, multiplexer_10_out,
       multiplexer_11_out, multiplexer_14_out, multiplexer_15_out, multiplexer_16_out, R1, R2, ram_1_data,
       shifter_1_out, SYSR1, SYSR2, WB_PC;
  wire [31:5] id_ex_1_out_47_2;
  wire [31:16] if_id_1_out_6_2;

  Clock #(.highDuration(1), .lowDuration(1)) clock_1 (.out(CLK));
  Button _1 (.out(IR1));
  Button _2 (.out(IR2));
  Button _3 (.out(IR3));
  Button \u_继续运行  (.out(Go));
  LED #(.active("true")) led_1 (.in(W1));
  LED #(.active("true")) led_2 (.in(W2));
  LED #(.active("true")) led_3 (.in(W3));
  Hex_Digit_Display hex_digit_display_1 (.value(LedData[31:28]));  // open: dp
  Hex_Digit_Display hex_digit_display_2 (.value(LedData[23:20]));  // open: dp
  Hex_Digit_Display hex_digit_display_3 (.value(LedData[27:24]));  // open: dp
  Multiplexer #(.select(1), .width(32), .disabled("Z"), .enable("false")) multiplexer_1 (
    .in0(adder_1_out), .in1({id_ex_1_out_47_2, id_ex_1_out_47}), .out(multiplexer_1_out), .sel(JR));
  Multiplexer #(.select(1), .width(32), .disabled("Z"), .enable("false")) multiplexer_2 (
    .in0(multiplexer_1_out), .in1({EX_PC[31:28], EXIR[25:0], 2'b00}), .out(multiplexer_2_out), .sel(JMP));
  Hex_Digit_Display hex_digit_display_4 (.value(LedData[19:16]));  // open: dp
  Hex_Digit_Display hex_digit_display_5 (.value(LedData[15:12]));  // open: dp
  Register #(.width(32), .trigger("rising"), .Select("low")) PC (
    .D(multiplexer_3_out), .en(Running), .Q(IF_PC), .clk(CLK), .clr(Go), .cs(dataCheck));  // open: preset
  Multiplexer #(.select(1), .width(32), .disabled("Z"), .enable("false")) multiplexer_3 (
    .in0(multiplexer_2_out), .in1(adder_2_out), .out(multiplexer_3_out), .sel(\有条件跳转 ));
  Hex_Digit_Display hex_digit_display_6 (.value(LedData[7:4]));  // open: dp
  Hex_Digit_Display hex_digit_display_7 (.value(LedData[11:8]));  // open: dp
  // Probe on \总周期数 
  Hex_Digit_Display hex_digit_display_8 (.value(LedData[3:0]));  // open: dp
  // Mips_Probe mips_probe_1: pin names not known; wires that end beside it: mips_probe_1_p1
  Adder #(.width(32)) adder_1 (.a(IF_PC), .b(32'h4), .out(adder_1_out));  // open: cin, cout
  // Probe on IF_PC[11:0]
  // Probe on ID_PC[11:0]
  ROM #(.addrWidth(10), .dataWidth(32), .Select("high")) rom_1 (.addr(IF_PC[11:2]), .data(mips_probe_1_p1));
  not not_1 (not_1_out, and_1_out);
  and and_1 (and_1_out, ~dataCheck, Running);  // AND_Gate
  \数据相关检测  \u_数据相关检测_1  (
    .in_1(A), .in_2(B), .in_3(EXWriteReg), .in_4(MEMWriteReg), .in_5(EXRegWrite), .in_6(MEMRegWrite),
    .in_7(R1_Used), .in_8(R2_Used), .out_10(dataCheck), .in_9(Running));
  // Probe on EX_PC[11:0]
  IF_ID if_id_1 (
    .in_1(CLK), .in_2(not_1_out), .in_3(or_1_out), .in_4(mips_probe_1_p1), .in_5(adder_1_out),
    .out_6({if_id_1_out_6_2, if_id_1_out_6}), .out_7(ID_PC));
  or or_1 (or_1_out, Go, \有条件跳转 , \无条件跳转 );
  // Probe on MEM_PC[11:0]
  // Probe on WB_PC[11:0]
  // Probe on {if_id_1_out_6_2, if_id_1_out_6}
  // Probe on if_id_1_out_6_2[31:26]
  // Probe on {if_id_1_out_6_2, if_id_1_out_6}
  \单周期硬布线控制器  \u_单周期硬布线控制器_1  (
    .Func(if_id_1_out_6[5:0]), .OP(if_id_1_out_6_2[31:26]), .ALU_OP(\单周期硬布线控制器_1_alu_op ),
    .MemToReg(\单周期硬布线控制器_1_memtoreg ), .MemWrite(\单周期硬布线控制器_1_memwrite ), .ALU_SRC(\单周期硬布线控制器_1_alu_src ),
    .RegWrite(\单周期硬布线控制器_1_regwrite ), .SysCALL(\单周期硬布线控制器_1_syscall ), .SignedExt(\单周期硬布线控制器_1_signedext ),
    .RegDst(\单周期硬布线控制器_1_regdst ), .JR(\单周期硬布线控制器_1_jr ), .JMP(\单周期硬布线控制器_1_jmp ), .Beq(\单周期硬布线控制器_1_beq ),
    .JAL(\单周期硬布线控制器_1_jal ), .Bne(\单周期硬布线控制器_1_bne ), .BLTZ(\单周期硬布线控制器_1_bltz ), .R1_Used(R1_Used),
    .R2_Used(R2_Used), .RS_SHAMT(\单周期硬布线控制器_1_rs_shamt ), .SB(\单周期硬布线控制器_1_sb ));
  Multiplexer #(.select(1), .width(5), .disabled("Z"), .enable("false")) multiplexer_4 (
    .in0(if_id_1_out_6_2[25:21]), .in1(5'b00010), .out(A), .sel(\单周期硬布线控制器_1_syscall ));
  Multiplexer #(.select(1), .width(5), .disabled("Z"), .enable("false")) multiplexer_5 (
    .in0(if_id_1_out_6_2[20:16]), .in1(5'b00100), .out(B), .sel(\单周期硬布线控制器_1_syscall ));
  Multiplexer #(.select(1), .width(5), .disabled("Z"), .enable("false")) multiplexer_6 (
    .in0(mem_wb_1_out_15[20:16]), .in1(mem_wb_1_out_15[15:11]), .out(multiplexer_6_out), .sel(RegDst));
  Multiplexer #(.select(1), .width(5), .disabled("Z"), .enable("false")) multiplexer_7 (
    .in0(multiplexer_6_out), .in1({5{1'b1}}), .out(multiplexer_7_out), .sel(JAL));
  Multiplexer #(.select(1), .width(32), .disabled("Z"), .enable("false")) multiplexer_8 (
    .in0(multiplexer_16_out), .in1(WB_PC), .out(multiplexer_8_out), .sel(JAL));
  // Probe on \总周期数 
  // Probe on \无条件分支数 
  // Probe on \条件分支成功数 
  // Probe on \插入气泡数 
  // Probe on \LoadUse次数 
  MIPS_Regifile mips_regifile_1 (
    .Din(multiplexer_8_out), .Clk(CLK), .R1(R1), .R2(R2), .WE(RegWrite), .W_num(multiplexer_7_out),
    .R1_num(A), .R2_num(B));
  or or_2 (\无条件跳转 , JR, JMP);
  not not_2 (not_2_out, Running);
  or or_3 (JMP, id_ex_1_out_37, id_ex_1_out_43);
  ID_EX id_ex_1 (
    .in_1(CLK), .in_2(not_2_out), .in_3(or_4_out), .in_4({if_id_1_out_6_2, if_id_1_out_6}), .in_5(ID_PC),
    .in_24(R1), .in_25(R2), .in_26(if_id_1_out_6), .in_8(\单周期硬布线控制器_1_memwrite ),
    .in_9(\单周期硬布线控制器_1_memtoreg ), .in_10(\单周期硬布线控制器_1_alu_op ), .in_11(\单周期硬布线控制器_1_alu_src ),
    .in_12(\单周期硬布线控制器_1_signedext ), .in_6(\单周期硬布线控制器_1_beq ), .in_7(\单周期硬布线控制器_1_bne ),
    .out_32(id_ex_1_out_32), .out_29(id_ex_1_out_29), .out_30(id_ex_1_out_30), .out_31(id_ex_1_out_31),
    .out_27(EXIR), .out_28(EX_PC), .out_47({id_ex_1_out_47_2, id_ex_1_out_47}), .out_48(id_ex_1_out_48),
    .out_49(id_ex_1_out_49), .out_34(id_ex_1_out_34), .out_35(id_ex_1_out_35), .out_33(id_ex_1_out_33),
    .in_13(\单周期硬布线控制器_1_regwrite ), .out_36(EXRegWrite), .in_14(\单周期硬布线控制器_1_jal ), .out_37(id_ex_1_out_37),
    .in_15(\单周期硬布线控制器_1_regdst ), .out_38(id_ex_1_out_38), .in_16(\单周期硬布线控制器_1_syscall ),
    .out_39(id_ex_1_out_39), .in_17(\单周期硬布线控制器_1_bltz ), .out_40(id_ex_1_out_40),
    .in_18(\单周期硬布线控制器_1_rs_shamt ), .out_41(id_ex_1_out_41), .in_19(\单周期硬布线控制器_1_sb ),
    .out_42(id_ex_1_out_42), .in_20(\单周期硬布线控制器_1_jmp ), .in_21(\单周期硬布线控制器_1_jr ), .out_43(id_ex_1_out_43),
    .out_44(JR));  // open: in_22, in_23, out_45, out_46
  or or_4 (or_4_out, \无条件跳转 , \有条件跳转 , Go, dataCheck);
  Multiplexer #(.select(1), .width(5), .disabled("Z"), .enable("false")) multiplexer_9 (
    .in0(EXIR[20:16]), .in1(EXIR[15:11]), .out(EXWriteReg), .sel(id_ex_1_out_38));
  assign bit_extender_1_out = {{16{1'b0}}, id_ex_1_out_49};  // Bit_Extender bit_extender_1
  Multiplexer #(.select(1), .width(32), .disabled("Z"), .enable("false")) multiplexer_10 (
    .in0(bit_extender_1_out), .in1(bit_extender_2_out), .out(multiplexer_10_out), .sel(id_ex_1_out_35));
  assign bit_extender_2_out = {{16{id_ex_1_out_49[15]}}, id_ex_1_out_49};  // Bit_Extender bit_extender_2
  // Probe on EXIR
  and and_2 (and_2_out, id_ex_1_out_40, id_ex_1_out_47_2[31]);
  Multiplexer #(.select(1), .width(32), .disabled("Z"), .enable("false")) multiplexer_11 (
    .in0(id_ex_1_out_48), .in1(multiplexer_10_out), .out(multiplexer_11_out), .sel(id_ex_1_out_34));
  or or_5 (\有条件跳转 , and_2_out, and_3_out, and_4_out);
  and and_3 (and_3_out, id_ex_1_out_29, mips_alu_1_equal);
  MIPS_ALU mips_alu_1 (
    .X({id_ex_1_out_47_2, id_ex_1_out_47}), .Y(multiplexer_11_out), .AluOP(id_ex_1_out_33),
    .Equal(mips_alu_1_equal), .Result(mips_alu_1_result), .shamt(multiplexer_12_out));  // open: Result_2
  Multiplexer #(.select(1), .width(5), .disabled("Z"), .enable("false")) multiplexer_12 (
    .in0(EXIR[10:6]), .in1(id_ex_1_out_47), .out(multiplexer_12_out), .sel(id_ex_1_out_41));
  Shifter #(.width(32), .shift("ll")) shifter_1 (.in(bit_extender_2_out), .\dist (5'b00010), .out(shifter_1_out));
  and and_4 (and_4_out, id_ex_1_out_30, ~mips_alu_1_equal);  // AND_Gate
  EX_MEM ex_mem_1 (
    .in_1(CLK), .in_2(not_3_out), .in_3(Go), .in_4(EXIR), .in_5(EX_PC), .in_6(id_ex_1_out_31),
    .in_7(id_ex_1_out_32), .in_9(id_ex_1_out_48), .in_10(mips_alu_1_result), .out_16(MEMIR), .out_17(MEM_PC),
    .out_21(ex_mem_1_out_21), .out_22(ex_mem_1_out_22), .out_18(ex_mem_1_out_18), .out_19(ex_mem_1_out_19),
    .in_11(EXRegWrite), .out_23(MEMRegWrite), .in_12(id_ex_1_out_37), .out_24(ex_mem_1_out_24),
    .in_13(id_ex_1_out_38), .out_25(ex_mem_1_out_25), .in_14(id_ex_1_out_39), .out_26(ex_mem_1_out_26),
    .in_15(id_ex_1_out_42), .out_27(ex_mem_1_out_27), .in_8({id_ex_1_out_47_2, id_ex_1_out_47}),
    .out_20(ex_mem_1_out_20));
  not not_3 (not_3_out, Running);
  Adder #(.width(32)) adder_2 (.a(shifter_1_out), .b(EX_PC), .out(adder_2_out));  // open: cin, cout
  // Probe on MEMIR
  Multiplexer #(.select(1), .width(5), .disabled("Z"), .enable("false")) multiplexer_13 (
    .in0(MEMIR[20:16]), .in1(MEMIR[15:11]), .out(MEMWriteReg), .sel(ex_mem_1_out_25));
  Multiplexer #(.select(1), .width(32), .disabled("Z"), .enable("false")) multiplexer_14 (
    .in0(ex_mem_1_out_21), .in1(multiplexer_15_out), .out(multiplexer_14_out), .sel(ex_mem_1_out_27));
  Multiplexer #(.select(2), .width(32), .disabled("Z"), .enable("false")) multiplexer_15 (
    .in0({ram_1_data[31:8], ex_mem_1_out_21[7:0]}),
    .in1({ram_1_data[31:16], ex_mem_1_out_21[7:0], ram_1_data[7:0]}),
    .in2({ram_1_data[31:24], ex_mem_1_out_21[7:0], ram_1_data[15:0]}),
    .in3({ex_mem_1_out_21[7:0], ram_1_data[23:0]}), .out(multiplexer_15_out), .sel(ex_mem_1_out_22[1:0]));
  RAM #(.addrWidth(10), .dataWidth(32), .bus("separate"), .Select("high")) ram_1 (
    .addr(ex_mem_1_out_22[11:2]), .din(multiplexer_14_out), .data(ram_1_data), .str(ex_mem_1_out_18),
    .sel(Running), .clk(CLK), .clr(Go));  // open: ld
  MEM_WB mem_wb_1 (
    .in_1(CLK), .in_2(not_4_out), .in_3(Go), .in_4(MEMIR), .in_5(MEM_PC), .in_9(ram_1_data),
    .in_6(ex_mem_1_out_19), .in_10(ex_mem_1_out_22), .out_15(mem_wb_1_out_15), .out_16(WB_PC),
    .out_20(mem_wb_1_out_20), .out_21(mem_wb_1_out_21), .out_17(mem_wb_1_out_17), .in_11(MEMRegWrite),
    .out_22(RegWrite), .in_12(ex_mem_1_out_24), .out_23(JAL), .in_13(ex_mem_1_out_25), .out_24(RegDst),
    .in_14(ex_mem_1_out_26), .out_25(Syscall), .in_7(ex_mem_1_out_20), .out_18(SYSR1),
    .in_8(ex_mem_1_out_21), .out_19(SYSR2));
  not not_4 (not_4_out, Running);
  Multiplexer #(.select(1), .width(32), .disabled("Z"), .enable("false")) multiplexer_16 (
    .in0(mem_wb_1_out_21), .in1(mem_wb_1_out_20), .out(multiplexer_16_out), .sel(mem_wb_1_out_17));
  // Probe on mem_wb_1_out_15
  Counter #(.width(16), .max('hffff), .ongoal("wrap"), .trigger("rising"), .behavior("old")) \u_无条件分支周期数  (
    .count(\无条件跳转 ), .Q(\无条件分支数 ), .clk(CLK), .clr(Go));  // open: load, D, carry, preset
  Counter #(.width(16), .max('hffff), .ongoal("wrap"), .trigger("rising"), .behavior("old")) \u_有条件分支周期数  (
    .count(\有条件跳转 ), .Q(\条件分支成功数 ), .clk(CLK), .clr(Go));  // open: load, D, carry, preset
  Comparator #(.width(32), .mode("twosComplement")) comparator_1 (
    .a(32'h22), .b(SYSR1), .eq(comparator_1_eq));  // open: gt, lt
  Counter #(.width(16), .max('hffff), .ongoal("wrap"), .trigger("rising"), .behavior("old")) \u_插入气泡数  (
    .count(dataCheck), .Q(\插入气泡数 ), .clk(CLK), .clr(Go));  // open: load, D, carry, preset
  and and_5 (and_5_out, comparator_1_eq, Syscall);
  not not_5 (not_5_out, comparator_1_eq);
  Register #(.width(32), .trigger("rising"), .Select("low")) register_1 (
    .D(SYSR2), .en(and_5_out), .Q(LedData), .clk(CLK), .clr(Go));
  D_Flip_Flop #(.trigger("falling"), .Pre_Clr_Positions("ABOVE_BELOW"), .NegatePresetClear("false"), .enable("true"), .NewFFLayout("true")) d_ff_1 (
    .clk(CLK), .D(not_5_out), .Qn(Running), .en(Syscall), .reset(Go));  // open: Q, preset
  Counter #(.width(16), .max('hffff), .ongoal("wrap"), .trigger("rising"), .behavior("old")) \u_总周期数  (
    .count(Running), .Q(\总周期数 ), .clk(CLK), .clr(Go));  // open: load, D, carry, preset

  // Other names for the same wires on the sheet: RST = Go

  // Notes on the sheet:
  //   中断源
  //   中断等待指示
  //   总复位信号应将除ROM以外所有存储组件全部清零
  //   数码管输出
  //   数码管输出应该用寄存器锁存，否则显示数据只能一闪而过
  //   指令存储器
  //   contents of rom_1 (hex, n*v repeats v):
  //   20110001 8000c05 20110001 20120002 20130003 8000c09 20110001 20120002 20130003 8000c0d 20110001
  //   20120002 20130003 8000c11 20110001 20120002 20130003 c000cb8 20100001 20110001 118fc0 112020
  //   20020022 c 118882 12200001 8000c15 112020 20020022 c 20110001 118880 112020 20020022 c 12200001
  //   8000c1f 20110001 118fc0 112020 20020022 c 1188c3 112020 20020022 c 118903 112020 20020022 c 118903
  //   112020 20020022 c 118903 112020 20020022 c 118903 112020 20020022 c 118903 112020 20020022 c 118903
  //   112020 20020022 c 118903 112020 20020022 c 20100001 109fc0 139fc3 8021 2012000c 24160003 26100001
  //   3210000f 20080008 20090001 139900 2709825 132020 20020022 c 1094022 1500fff9 22100001 2018000f
  //   2188024 108700 20080008 20090001 139902 2709825 132021 20020022 c 1094022 1500fff9 108702 2c9b022
  //   12c00001 8000c50 4020 1084027 84400 3508ffff 82021 20020022 c 2010ffff 20110000 ae300000 22100001
  //   22310004 ae300000 22100001 22310004 ae300000 22100001 22310004 ae300000 22100001 22310004 ae300000
  //   22100001 22310004 ae300000 22100001 22310004 ae300000 22100001 22310004 ae300000 22100001 22310004
  //   ae300000 22100001 22310004 ae300000 22100001 22310004 ae300000 22100001 22310004 ae300000 22100001
  //   22310004 ae300000 22100001 22310004 ae300000 22100001 22310004 ae300000 22100001 22310004 ae300000
  //   22100001 22310004 22100001 8020 2011003c 8e130000 8e340000 274402a 11000002 ae330000 ae140000
  //   2231fffc 1611fff8 102020 20020022 c 22100004 2011003c 1611fff2 20020032 c 20100000 22100001 102020
  //   20020022 c 22100002 102020 20020022 c 22100003 102020 20020022 c 22100004 102020 20020022 c 22100005
  //   102020 20020022 c 22100006 102020 20020022 c 22100007 102020 20020022 c 22100008 102020 20020022
  //   20020022 c 3e00008
  //   OP
  //   OP
  //   Func
  //   Func
  //   rs
  //   rt
  //   rd
  //   Beq
  //   Bne
  //   BLTZ
  //   MemToReg
  //   MemWrite
  //   AluOP
  //   AluSrcB
  //   RegWrite
  //   JAL
endmodule

module \重定向流水线  (
);

  wire and_1_out, and_2_out, and_3_out, and_4_out, and_5_out, CLK, comparator_1_eq, ex_mem_1_out_18,
       ex_mem_1_out_24, ex_mem_1_out_25, ex_mem_1_out_26, ex_mem_1_out_27, EXMemToReg, EXRegWrite, Go,
       id_ex_1_out_29, id_ex_1_out_30, id_ex_1_out_31, id_ex_1_out_34, id_ex_1_out_35, id_ex_1_out_37,
       id_ex_1_out_38, id_ex_1_out_39, id_ex_1_out_40, id_ex_1_out_41, id_ex_1_out_42, id_ex_1_out_43, IR1,
       IR2, IR3, JAL, JMP, JR, LoadUse, mem_wb_1_out_17, MEMMemToReg, MEMRegWrite, mips_alu_1_equal,
       not_1_out, not_2_out, not_3_out, not_4_out, not_5_out, or_1_out, or_4_out, R1_Used, R2_Used, RegDst,
       RegWrite, Running, Syscall, W1, W2, W3, \单周期硬布线控制器_1_alu_src , \单周期硬布线控制器_1_beq , \单周期硬布线控制器_1_bltz ,
       \单周期硬布线控制器_1_bne , \单周期硬布线控制器_1_jal , \单周期硬布线控制器_1_jmp , \单周期硬布线控制器_1_jr , \单周期硬布线控制器_1_memtoreg ,
       \单周期硬布线控制器_1_memwrite , \单周期硬布线控制器_1_regdst , \单周期硬布线控制器_1_regwrite , \单周期硬布线控制器_1_rs_shamt ,
       \单周期硬布线控制器_1_sb , \单周期硬布线控制器_1_signedext , \单周期硬布线控制器_1_syscall , \无条件跳转 , \有条件跳转 ;
  wire [1:0] ASel, BSel, id_ex_1_out_45, id_ex_1_out_46;
  wire [3:0] id_ex_1_out_33, \单周期硬布线控制器_1_alu_op ;
  wire [4:0] A, B, EXWriteReg, MEMWriteReg, multiplexer_6_out, multiplexer_7_out, multiplexer_14_out;
  wire [15:0] id_ex_1_out_49, if_id_1_out_6, \LoadUse次数 , \总周期数 , \插入气泡数 , \无条件分支数 , \条件分支成功数 ;
  wire [23:0] ram_1_data;
  wire [23:16] ram_1_data_2;
  wire [31:0] adder_1_out, adder_2_out, bit_extender_1_out, bit_extender_2_out, ex_mem_1_out_20,
       ex_mem_1_out_21, ex_mem_1_out_22, EX_PC, EXIR, id_ex_1_out_47, id_ex_1_out_48, ID_PC, IF_PC, LedData,
       MEM_PC, mem_wb_1_out_15, mem_wb_1_out_20, mem_wb_1_out_21, MEMIR, mips_alu_1_result, mips_probe_1_p1,
       multiplexer_1_out, multiplexer_2_out, multiplexer_3_out, multiplexer_8_out, multiplexer_10_out,
       multiplexer_11_out, multiplexer_12_out, multiplexer_13_out, multiplexer_16_out, multiplexer_17_out,
       multiplexer_18_out, R1, R2, shifter_1_out, SYSR1, SYSR2, WB_PC;
  wire [31:16] if_id_1_out_6_2;

  Clock #(.highDuration(1), .lowDuration(1)) clock_1 (.out(CLK));
  Button _1 (.out(IR1));
  Button _2 (.out(IR2));
  Button _3 (.out(IR3));
  Button \u_继续运行  (.out(Go));
  LED #(.active("true")) led_1 (.in(W1));
  LED #(.active("true")) led_2 (.in(W2));
  LED #(.active("true")) led_3 (.in(W3));
  Hex_Digit_Display hex_digit_display_1 (.value(LedData[31:28]));  // open: dp
  Hex_Digit_Display hex_digit_display_2 (.value(LedData[23:20]));  // open: dp
  Hex_Digit_Display hex_digit_display_3 (.value(LedData[27:24]));  // open: dp
  Multiplexer #(.select(1), .width(32), .disabled("Z"), .enable("false")) multiplexer_1 (
    .in0(adder_1_out), .in1(id_ex_1_out_47), .out(multiplexer_1_out), .sel(JR));
  Multiplexer #(.select(1), .width(32), .disabled("Z"), .enable("false")) multiplexer_2 (
    .in0(multiplexer_1_out), .in1({EX_PC[31:28], EXIR[25:0], 2'b00}), .out(multiplexer_2_out), .sel(JMP));
  Hex_Digit_Display hex_digit_display_4 (.value(LedData[19:16]));  // open: dp
  Hex_Digit_Display hex_digit_display_5 (.value(LedData[15:12]));  // open: dp
  Register #(.width(32), .trigger("rising"), .Select("low")) PC (
    .D(multiplexer_3_out), .en(Running), .Q(IF_PC), .clk(CLK), .clr(Go), .cs(LoadUse));  // open: preset
  Multiplexer #(.select(1), .width(32), .disabled("Z"), .enable("false")) multiplexer_3 (
    .in0(multiplexer_2_out), .in1(adder_2_out), .out(multiplexer_3_out), .sel(\有条件跳转 ));
  Hex_Digit_Display hex_digit_display_6 (.value(LedData[7:4]));  // open: dp
  Hex_Digit_Display hex_digit_display_7 (.value(LedData[11:8]));  // open: dp
  // Probe on \总周期数 
  Hex_Digit_Display hex_digit_display_8 (.value(LedData[3:0]));  // open: dp
  // Mips_Probe mips_probe_1: pin names not known; wires that end beside it: mips_probe_1_p1
  Adder #(.width(32)) adder_1 (.a(IF_PC), .b(32'h4), .out(adder_1_out));  // open: cin, cout
  // Probe on ID_PC[11:0]
  // Probe on IF_PC[11:0]
  ROM #(.addrWidth(10), .dataWidth(32), .Select("high")) rom_1 (.addr(IF_PC[11:2]), .data(mips_probe_1_p1));
  not not_1 (not_1_out, and_1_out);
  and and_1 (and_1_out, ~LoadUse, Running);  // AND_Gate
  \重定向数据相关检测  \u_重定向数据相关检测_1  (
    .in_1(A), .out_12(ASel), .in_2(B), .out_13(BSel), .in_3(EXWriteReg), .out_14(LoadUse),
    .in_4(MEMWriteReg), .in_5(EXRegWrite), .in_6(MEMRegWrite), .in_7(EXMemToReg), .in_8(R1_Used),
    .in_9(R2_Used), .in_10(Running), .in_11(MEMMemToReg));
  // Probe on EX_PC[11:0]
  IF_ID if_id_1 (
    .in_1(CLK), .in_2(not_1_out), .in_3(or_1_out), .in_4(mips_probe_1_p1), .in_5(adder_1_out),
    .out_6({if_id_1_out_6_2, if_id_1_out_6}), .out_7(ID_PC));
  or or_1 (or_1_out, Go, \有条件跳转 , \无条件跳转 );
  // Probe on MEM_PC[11:0]
  // Probe on WB_PC[11:0]
  // Probe on {if_id_1_out_6_2, if_id_1_out_6}
  // Probe on if_id_1_out_6_2[31:26]
  // Probe on {if_id_1_out_6_2, if_id_1_out_6}
  \单周期硬布线控制器  \u_单周期硬布线控制器_1  (
    .Func(if_id_1_out_6[5:0]), .OP(if_id_1_out_6_2[31:26]), .ALU_OP(\单周期硬布线控制器_1_alu_op ),
    .MemToReg(\单周期硬布线控制器_1_memtoreg ), .MemWrite(\单周期硬布线控制器_1_memwrite ), .ALU_SRC(\单周期硬布线控制器_1_alu_src ),
    .RegWrite(\单周期硬布线控制器_1_regwrite ), .SysCALL(\单周期硬布线控制器_1_syscall ), .SignedExt(\单周期硬布线控制器_1_signedext ),
    .RegDst(\单周期硬布线控制器_1_regdst ), .JR(\单周期硬布线控制器_1_jr ), .JMP(\单周期硬布线控制器_1_jmp ), .Beq(\单周期硬布线控制器_1_beq ),
    .JAL(\单周期硬布线控制器_1_jal ), .Bne(\单周期硬布线控制器_1_bne ), .BLTZ(\单周期硬布线控制器_1_bltz ), .R1_Used(R1_Used),
    .R2_Used(R2_Used), .RS_SHAMT(\单周期硬布线控制器_1_rs_shamt ), .SB(\单周期硬布线控制器_1_sb ));
  Multiplexer #(.select(1), .width(5), .disabled("Z"), .enable("false")) multiplexer_4 (
    .in0(if_id_1_out_6_2[25:21]), .in1(5'b00010), .out(A), .sel(\单周期硬布线控制器_1_syscall ));
  Multiplexer #(.select(1), .width(5), .disabled("Z"), .enable("false")) multiplexer_5 (
    .in0(if_id_1_out_6_2[20:16]), .in1(5'b00100), .out(B), .sel(\单周期硬布线控制器_1_syscall ));
  Multiplexer #(.select(1), .width(5), .disabled("Z"), .enable("false")) multiplexer_6 (
    .in0(mem_wb_1_out_15[20:16]), .in1(mem_wb_1_out_15[15:11]), .out(multiplexer_6_out), .sel(RegDst));
  Multiplexer #(.select(1), .width(5), .disabled("Z"), .enable("false")) multiplexer_7 (
    .in0(multiplexer_6_out), .in1({5{1'b1}}), .out(multiplexer_7_out), .sel(JAL));
  Multiplexer #(.select(1), .width(32), .disabled("Z"), .enable("false")) multiplexer_8 (
    .in0(multiplexer_18_out), .in1(WB_PC), .out(multiplexer_8_out), .sel(JAL));
  // Probe on \总周期数 
  // Probe on \无条件分支数 
  // Probe on \条件分支成功数 
  // Probe on \插入气泡数 
  // Probe on \LoadUse次数 
  MIPS_Regifile mips_regifile_1 (
    .Din(multiplexer_8_out), .Clk(CLK), .R1(R1), .R2(R2), .WE(RegWrite), .W_num(multiplexer_7_out),
    .R1_num(A), .R2_num(B));
  or or_2 (\无条件跳转 , JR, JMP);
  not not_2 (not_2_out, Running);
  or or_3 (JMP, id_ex_1_out_37, id_ex_1_out_43);
  ID_EX id_ex_1 (
    .in_1(CLK), .in_2(not_2_out), .in_3(or_4_out), .in_4({if_id_1_out_6_2, if_id_1_out_6}), .in_5(ID_PC),
    .in_24(R1), .in_25(R2), .in_26(if_id_1_out_6), .in_8(\单周期硬布线控制器_1_memwrite ),
    .in_9(\单周期硬布线控制器_1_memtoreg ), .in_10(\单周期硬布线控制器_1_alu_op ), .in_11(\单周期硬布线控制器_1_alu_src ),
    .in_12(\单周期硬布线控制器_1_signedext ), .in_6(\单周期硬布线控制器_1_beq ), .in_7(\单周期硬布线控制器_1_bne ), .out_32(EXMemToReg),
    .out_29(id_ex_1_out_29), .out_30(id_ex_1_out_30), .out_31(id_ex_1_out_31), .out_27(EXIR), .out_28(EX_PC),
    .out_47(id_ex_1_out_47), .out_48(id_ex_1_out_48), .out_49(id_ex_1_out_49), .out_34(id_ex_1_out_34),
    .out_35(id_ex_1_out_35), .out_33(id_ex_1_out_33), .in_13(\单周期硬布线控制器_1_regwrite ), .out_36(EXRegWrite),
    .in_14(\单周期硬布线控制器_1_jal ), .out_37(id_ex_1_out_37), .in_15(\单周期硬布线控制器_1_regdst ),
    .out_38(id_ex_1_out_38), .in_16(\单周期硬布线控制器_1_syscall ), .out_39(id_ex_1_out_39),
    .in_17(\单周期硬布线控制器_1_bltz ), .out_40(id_ex_1_out_40), .in_18(\单周期硬布线控制器_1_rs_shamt ),
    .out_41(id_ex_1_out_41), .in_19(\单周期硬布线控制器_1_sb ), .out_42(id_ex_1_out_42), .in_20(\单周期硬布线控制器_1_jmp ),
    .in_21(\单周期硬布线控制器_1_jr ), .out_43(id_ex_1_out_43), .out_44(JR), .in_22(ASel), .in_23(BSel),
    .out_45(id_ex_1_out_45), .out_46(id_ex_1_out_46));
  or or_4 (or_4_out, \无条件跳转 , \有条件跳转 , Go, LoadUse);
  Multiplexer #(.select(1), .width(5), .disabled("Z"), .enable("false")) multiplexer_9 (
    .in0(EXIR[20:16]), .in1(EXIR[15:11]), .out(EXWriteReg), .sel(id_ex_1_out_38));
  assign bit_extender_1_out = {{16{1'b0}}, id_ex_1_out_49};  // Bit_Extender bit_extender_1
  Multiplexer #(.select(1), .width(32), .disabled("Z"), .enable("false")) multiplexer_10 (
    .in0(bit_extender_1_out), .in1(bit_extender_2_out), .out(multiplexer_10_out), .sel(id_ex_1_out_35));
  assign bit_extender_2_out = {{16{id_ex_1_out_49[15]}}, id_ex_1_out_49};  // Bit_Extender bit_extender_2
  and and_2 (and_2_out, id_ex_1_out_40, id_ex_1_out_47[31]);
  Multiplexer #(.select(2), .width(32), .disabled("Z"), .enable("false")) multiplexer_11 (
    .in0(id_ex_1_out_47), .in1(ex_mem_1_out_22), .in2(mem_wb_1_out_21), .in3(mem_wb_1_out_20),
    .out(multiplexer_11_out), .sel(id_ex_1_out_45));
  Multiplexer #(.select(2), .width(32), .disabled("Z"), .enable("false")) multiplexer_12 (
    .in0(id_ex_1_out_48), .in1(ex_mem_1_out_22), .in2(mem_wb_1_out_21), .in3(mem_wb_1_out_20),
    .out(multiplexer_12_out), .sel(id_ex_1_out_46));
  or or_5 (\有条件跳转 , and_2_out, and_3_out, and_4_out);
  and and_3 (and_3_out, id_ex_1_out_29, mips_alu_1_equal);
  Multiplexer #(.select(1), .width(32), .disabled("Z"), .enable("false")) multiplexer_13 (
    .in0(multiplexer_12_out), .in1(multiplexer_10_out), .out(multiplexer_13_out), .sel(id_ex_1_out_34));
  Multiplexer #(.select(1), .width(5), .disabled("Z"), .enable("false")) multiplexer_14 (
    .in0(EXIR[10:6]), .in1(id_ex_1_out_47[4:0]), .out(multiplexer_14_out), .sel(id_ex_1_out_41));
  Shifter #(.width(32), .shift("ll")) shifter_1 (.in(bit_extender_2_out), .\dist (5'b00010), .out(shifter_1_out));
  and and_4 (and_4_out, id_ex_1_out_30, ~mips_alu_1_equal);  // AND_Gate
  EX_MEM ex_mem_1 (
    .in_1(CLK), .in_2(not_3_out), .in_3(Go), .in_4(EXIR), .in_5(EX_PC), .in_6(id_ex_1_out_31),
    .in_7(EXMemToReg), .in_9(id_ex_1_out_48), .in_10(mips_alu_1_result), .out_16(MEMIR), .out_17(MEM_PC),
    .out_21(ex_mem_1_out_21), .out_22(ex_mem_1_out_22), .out_18(ex_mem_1_out_18), .out_19(MEMMemToReg),
    .in_11(EXRegWrite), .out_23(MEMRegWrite), .in_12(id_ex_1_out_37), .out_24(ex_mem_1_out_24),
    .in_13(id_ex_1_out_38), .out_25(ex_mem_1_out_25), .in_14(id_ex_1_out_39), .out_26(ex_mem_1_out_26),
    .in_15(id_ex_1_out_42), .out_27(ex_mem_1_out_27), .in_8(multiplexer_11_out), .out_20(ex_mem_1_out_20));
  MIPS_ALU mips_alu_1 (
    .X(multiplexer_11_out), .Y(multiplexer_13_out), .AluOP(id_ex_1_out_33), .Equal(mips_alu_1_equal),
    .Result(mips_alu_1_result), .shamt(multiplexer_14_out));  // open: Result_2
  not not_3 (not_3_out, Running);
  Adder #(.width(32)) adder_2 (.a(shifter_1_out), .b(EX_PC), .out(adder_2_out));  // open: cin, cout
  Multiplexer #(.select(1), .width(5), .disabled("Z"), .enable("false")) multiplexer_15 (
    .in0(MEMIR[20:16]), .in1(MEMIR[15:11]), .out(MEMWriteReg), .sel(ex_mem_1_out_25));
  // Probe on MEMIR
  Multiplexer #(.select(2), .width(32), .disabled("Z"), .enable("false")) multiplexer_16 (
    .in0({ram_1_data_2, ram_1_data[23:8], ex_mem_1_out_21[7:0]}),
    .in1({ram_1_data_2, ram_1_data[23:16], ex_mem_1_out_21[7:0], ram_1_data[7:0]}),
    .in2({ram_1_data_2, ex_mem_1_out_21[7:0], ram_1_data[15:0]}), .in3({ex_mem_1_out_21[7:0], ram_1_data}),
    .out(multiplexer_16_out), .sel(ex_mem_1_out_22[1:0]));
  Multiplexer #(.select(1), .width(32), .disabled("Z"), .enable("false")) multiplexer_17 (
    .in0(ex_mem_1_out_21), .in1(multiplexer_16_out), .out(multiplexer_17_out), .sel(ex_mem_1_out_27));
  MEM_WB mem_wb_1 (
    .in_1(CLK), .in_2(not_4_out), .in_3(Go), .in_4(MEMIR), .in_5(MEM_PC), .in_9({ram_1_data_2, ram_1_data}),
    .in_6(MEMMemToReg), .in_10(ex_mem_1_out_22), .out_15(mem_wb_1_out_15), .out_16(WB_PC),
    .out_20(mem_wb_1_out_20), .out_21(mem_wb_1_out_21), .out_17(mem_wb_1_out_17), .in_11(MEMRegWrite),
    .out_22(RegWrite), .in_12(ex_mem_1_out_24), .out_23(JAL), .in_13(ex_mem_1_out_25), .out_24(RegDst),
    .in_14(ex_mem_1_out_26), .out_25(Syscall), .in_7(ex_mem_1_out_20), .out_18(SYSR1),
    .in_8(ex_mem_1_out_21), .out_19(SYSR2));
  RAM #(.addrWidth(10), .dataWidth(32), .bus("separate"), .Select("high")) ram_1 (
    .addr(ex_mem_1_out_22[11:2]), .din(multiplexer_17_out), .data({ram_1_data_2, ram_1_data}),
    .str(ex_mem_1_out_18), .sel(Running), .clk(CLK), .clr(Go));  // open: ld
  not not_4 (not_4_out, Running);
  Multiplexer #(.select(1), .width(32), .disabled("Z"), .enable("false")) multiplexer_18 (
    .in0(mem_wb_1_out_21), .in1(mem_wb_1_out_20), .out(multiplexer_18_out), .sel(mem_wb_1_out_17));
  Counter #(.width(16), .max('hffff), .ongoal("wrap"), .trigger("rising"), .behavior("old")) \u_无条件分支周期数  (
    .count(\无条件跳转 ), .Q(\无条件分支数 ), .clk(CLK), .clr(Go));  // open: load, D, carry, preset
  Counter #(.width(16), .max('hffff), .ongoal("wrap"), .trigger("rising"), .behavior("old")) \u_有条件分支周期数  (
    .count(\有条件跳转 ), .Q(\条件分支成功数 ), .clk(CLK), .clr(Go));  // open: load, D, carry, preset
  Counter #(.width(16), .max('hffff), .ongoal("wrap"), .trigger("rising"), .behavior("old")) \LoadUse数  (
    .count(LoadUse), .Q(\LoadUse次数 ), .clk(CLK), .clr(Go));  // open: load, D, carry, preset
  Comparator #(.width(32), .mode("twosComplement")) comparator_1 (
    .a(32'h22), .b(SYSR1), .eq(comparator_1_eq));  // open: gt, lt
  and and_5 (and_5_out, comparator_1_eq, Syscall);
  not not_5 (not_5_out, comparator_1_eq);
  Register #(.width(32), .trigger("rising"), .Select("low")) register_1 (
    .D(SYSR2), .en(and_5_out), .Q(LedData), .clk(CLK), .clr(Go));
  D_Flip_Flop #(.trigger("falling"), .Pre_Clr_Positions("ABOVE_BELOW"), .NegatePresetClear("false"), .enable("true"), .NewFFLayout("true")) d_ff_1 (
    .clk(CLK), .D(not_5_out), .Qn(Running), .en(Syscall), .reset(Go));  // open: Q, preset
  Counter #(.width(16), .max('hffff), .ongoal("wrap"), .trigger("rising"), .behavior("old")) \u_总周期数  (
    .count(Running), .Q(\总周期数 ), .clk(CLK), .clr(Go));  // open: load, D, carry, preset

  // Other names for the same wires on the sheet: RST = Go

  // Notes on the sheet:
  //   中断源
  //   中断等待指示
  //   总复位信号应将除ROM以外所有存储组件全部清零
  //   数码管输出
  //   数码管输出应该用寄存器锁存，否则显示数据只能一闪而过
  //   指令存储器
  //   contents of rom_1 (hex, n*v repeats v):
  //   20110001 8000c05 20110001 20120002 20130003 8000c09 20110001 20120002 20130003 8000c0d 20110001
  //   20120002 20130003 8000c11 20110001 20120002 20130003 c000cb8 20100001 20110001 118fc0 112020
  //   20020022 c 118882 12200001 8000c15 112020 20020022 c 20110001 118880 112020 20020022 c 12200001
  //   8000c1f 20110001 118fc0 112020 20020022 c 1188c3 112020 20020022 c 118903 112020 20020022 c 118903
  //   112020 20020022 c 118903 112020 20020022 c 118903 112020 20020022 c 118903 112020 20020022 c 118903
  //   112020 20020022 c 118903 112020 20020022 c 20100001 109fc0 139fc3 8021 2012000c 24160003 26100001
  //   3210000f 20080008 20090001 139900 2709825 132020 20020022 c 1094022 1500fff9 22100001 2018000f
  //   2188024 108700 20080008 20090001 139902 2709825 132021 20020022 c 1094022 1500fff9 108702 2c9b022
  //   12c00001 8000c50 4020 1084027 84400 3508ffff 82021 20020022 c 2010ffff 20110000 ae300000 22100001
  //   22310004 ae300000 22100001 22310004 ae300000 22100001 22310004 ae300000 22100001 22310004 ae300000
  //   22100001 22310004 ae300000 22100001 22310004 ae300000 22100001 22310004 ae300000 22100001 22310004
  //   ae300000 22100001 22310004 ae300000 22100001 22310004 ae300000 22100001 22310004 ae300000 22100001
  //   22310004 ae300000 22100001 22310004 ae300000 22100001 22310004 ae300000 22100001 22310004 ae300000
  //   22100001 22310004 22100001 8020 2011003c 8e130000 8e340000 274402a 11000002 ae330000 ae140000
  //   2231fffc 1611fff8 102020 20020022 c 22100004 2011003c 1611fff2 20020032 c 20100000 22100001 102020
  //   20020022 c 22100002 102020 20020022 c 22100003 102020 20020022 c 22100004 102020 20020022 c 22100005
  //   102020 20020022 c 22100006 102020 20020022 c 22100007 102020 20020022 c 22100008 102020 20020022
  //   20020022 c 3e00008
  //   OP
  //   OP
  //   Func
  //   Func
  //   rs
  //   rt
  //   rd
  //   Beq
  //   Bne
  //   BLTZ
  //   MemToReg
  //   MemWrite
  //   AluOP
  //   AluSrcB
  //   RegWrite
  //   JAL
endmodule

module \中断按键参考电路  (
  input  \同步清零信号 ,
  output \与中断屏蔽位与 
);

  wire \_1号中断_out , and_1_out, clock_1_out, d_ff_1_q, or_1_out, or_2_out;

  Clock #(.highDuration(1), .lowDuration(1)) clock_1 (.out(clock_1_out));
  Button \_1号中断  (.out(\_1号中断_out ));
  LED #(.active("true")) \_1号中断等待指示灯  (.in(or_1_out));
  or or_1 (or_1_out, \与中断屏蔽位与 , d_ff_1_q);
  D_Flip_Flop #(.trigger("rising"), .Pre_Clr_Positions("LEGACY"), .NegatePresetClear("false"), .enable("true"), .NewFFLayout("false")) d_ff_1 (
    .clk(\_1号中断_out ), .D(1'b1), .Q(d_ff_1_q), .reset(\与中断屏蔽位与 ));  // open: Qn, preset, en
  or or_2 (or_2_out, d_ff_1_q, \与中断屏蔽位与 );
  and and_1 (and_1_out, or_2_out, ~\同步清零信号 );  // AND_Gate
  D_Flip_Flop #(.trigger("rising"), .Pre_Clr_Positions("LEGACY"), .NegatePresetClear("false"), .enable("true"), .NewFFLayout("false")) IR1 (
    .clk(clock_1_out), .D(and_1_out), .Q(\与中断屏蔽位与 ));  // open: Qn, preset, en, reset

  // Notes on the sheet:
  //   中断信号采样参考电路
  //   Reset 
endmodule

module IF_ID (
  input  in_1,
  input  in_2,
  input  in_3,
  input  [31:0] in_4,
  input  [31:0] in_5,
  output [31:0] out_6,
  output [31:0] out_7
);

  wire pull_resistor_2_node;
  wire [31:0] multiplexer_1_out, multiplexer_2_out;

  Multiplexer #(.select(1), .width(32), .disabled("Z"), .enable("false")) multiplexer_1 (
    .in0(in_4), .in1({32{1'b0}}), .out(multiplexer_1_out), .sel(in_3));
  Multiplexer #(.select(1), .width(32), .disabled("Z"), .enable("false")) multiplexer_2 (
    .in0(in_5), .in1({32{1'b0}}), .out(multiplexer_2_out), .sel(in_3));
  Pull_Resistor #(.pull(0)) pull_resistor_1 (.node(in_3));
  Pull_Resistor #(.pull(0)) pull_resistor_2 (.node(pull_resistor_2_node));
  not not_1 (pull_resistor_2_node, in_2);
  Register #(.width(32), .trigger("rising"), .Select("low")) register_1 (
    .D(multiplexer_1_out), .en(pull_resistor_2_node), .Q(out_6), .clk(in_1));  // open: clr
  Register #(.width(32), .trigger("rising"), .Select("low")) register_2 (
    .D(multiplexer_2_out), .en(pull_resistor_2_node), .Q(out_7), .clk(in_1));  // open: clr

  // Other names for the same wires on the sheet: Clear = in_3; Clk = in_1; Enable = in_2; IRIn[31:0] = in_4;
  //   IROut[31:0] = out_6; PCIn[31:0] = in_5; PCOut[31:0] = out_7
endmodule

module ID_EX (
  input  in_1,
  input  in_2,
  input  in_3,
  input  [31:0] in_4,
  input  [31:0] in_5,
  input  in_6,
  input  in_7,
  input  in_8,
  input  in_9,
  input  [3:0] in_10,
  input  in_11,
  input  in_12,
  input  in_13,
  input  in_14,
  input  in_15,
  input  in_16,
  input  in_17,
  input  in_18,
  input  in_19,
  input  in_20,
  input  in_21,
  input  [1:0] in_22,
  input  [1:0] in_23,
  input  [31:0] in_24,
  input  [31:0] in_25,
  input  [15:0] in_26,
  output [31:0] out_27,
  output [31:0] out_28,
  output out_29,
  output out_30,
  output out_31,
  output out_32,
  output [3:0] out_33,
  output out_34,
  output out_35,
  output out_36,
  output out_37,
  output out_38,
  output out_39,
  output out_40,
  output out_41,
  output out_42,
  output out_43,
  output out_44,
  output [1:0] out_45,
  output [1:0] out_46,
  output [31:0] out_47,
  output [31:0] out_48,
  output [15:0] out_49
);

  wire multiplexer_1_out, multiplexer_2_out, multiplexer_3_out, multiplexer_4_out, multiplexer_6_out,
       multiplexer_7_out, multiplexer_8_out, multiplexer_9_out, multiplexer_10_out, multiplexer_11_out,
       multiplexer_12_out, multiplexer_13_out, multiplexer_14_out, multiplexer_15_out, multiplexer_18_out,
       pull_resistor_2_node;
  wire [1:0] multiplexer_16_out, multiplexer_17_out;
  wire [3:0] multiplexer_5_out;
  wire [15:0] multiplexer_23_out;
  wire [31:0] multiplexer_19_out, multiplexer_20_out, multiplexer_21_out, multiplexer_22_out;

  Multiplexer #(.select(1), .width(1), .disabled("Z"), .enable("false")) multiplexer_1 (
    .in0(in_6), .in1(1'b0), .out(multiplexer_1_out), .sel(in_3));
  Multiplexer #(.select(1), .width(1), .disabled("Z"), .enable("false")) multiplexer_2 (
    .in0(in_7), .in1(1'b0), .out(multiplexer_2_out), .sel(in_3));
  Multiplexer #(.select(1), .width(1), .disabled("Z"), .enable("false")) multiplexer_3 (
    .in0(in_8), .in1(1'b0), .out(multiplexer_3_out), .sel(in_3));
  Multiplexer #(.select(1), .width(1), .disabled("Z"), .enable("false")) multiplexer_4 (
    .in0(in_9), .in1(1'b0), .out(multiplexer_4_out), .sel(in_3));
  Multiplexer #(.select(1), .width(4), .disabled("Z"), .enable("false")) multiplexer_5 (
    .in0(in_10), .in1(4'b0000), .out(multiplexer_5_out), .sel(in_3));
  Multiplexer #(.select(1), .width(1), .disabled("Z"), .enable("false")) multiplexer_6 (
    .in0(in_11), .in1(1'b0), .out(multiplexer_6_out), .sel(in_3));
  Multiplexer #(.select(1), .width(1), .disabled("Z"), .enable("false")) multiplexer_7 (
    .in0(in_12), .in1(1'b0), .out(multiplexer_7_out), .sel(in_3));
  Multiplexer #(.select(1), .width(1), .disabled("Z"), .enable("false")) multiplexer_8 (
    .in0(in_13), .in1(1'b0), .out(multiplexer_8_out), .sel(in_3));
  Multiplexer #(.select(1), .width(1), .disabled("Z"), .enable("false")) multiplexer_9 (
    .in0(in_14), .in1(1'b0), .out(multiplexer_9_out), .sel(in_3));
  Multiplexer #(.select(1), .width(1), .disabled("Z"), .enable("false")) multiplexer_10 (
    .in0(in_15), .in1(1'b0), .out(multiplexer_10_out), .sel(in_3));
  Multiplexer #(.select(1), .width(1), .disabled("Z"), .enable("false")) multiplexer_11 (
    .in0(in_16), .in1(1'b0), .out(multiplexer_11_out), .sel(in_3));
  Multiplexer #(.select(1), .width(1), .disabled("Z"), .enable("false")) multiplexer_12 (
    .in0(in_17), .in1(1'b0), .out(multiplexer_12_out), .sel(in_3));
  Multiplexer #(.select(1), .width(1), .disabled("Z"), .enable("false")) multiplexer_13 (
    .in0(in_18), .in1(1'b0), .out(multiplexer_13_out), .sel(in_3));
  Multiplexer #(.select(1), .width(1), .disabled("Z"), .enable("false")) multiplexer_14 (
    .in0(in_20), .in1(1'b0), .out(multiplexer_14_out), .sel(in_3));
  Multiplexer #(.select(1), .width(1), .disabled("Z"), .enable("false")) multiplexer_15 (
    .in0(in_21), .in1(1'b0), .out(multiplexer_15_out), .sel(in_3));
  Multiplexer #(.select(1), .width(2), .disabled("Z"), .enable("false")) multiplexer_16 (
    .in0(in_22), .in1(2'b00), .out(multiplexer_16_out), .sel(in_3));
  Multiplexer #(.select(1), .width(2), .disabled("Z"), .enable("false")) multiplexer_17 (
    .in0(in_23), .in1(2'b00), .out(multiplexer_17_out), .sel(in_3));
  Multiplexer #(.select(1), .width(1), .disabled("Z"), .enable("false")) multiplexer_18 (
    .in0(in_19), .in1(1'b0), .out(multiplexer_18_out), .sel(in_3));
  Multiplexer #(.select(1), .width(32), .disabled("Z"), .enable("false")) multiplexer_19 (
    .in0(in_4), .in1({32{1'b0}}), .out(multiplexer_19_out), .sel(in_3));
  Multiplexer #(.select(1), .width(32), .disabled("Z"), .enable("false")) multiplexer_20 (
    .in0(in_5), .in1({32{1'b0}}), .out(multiplexer_20_out), .sel(in_3));
  Multiplexer #(.select(1), .width(32), .disabled("Z"), .enable("false")) multiplexer_21 (
    .in0(in_24), .in1({32{1'b0}}), .out(multiplexer_21_out), .sel(in_3));
  Multiplexer #(.select(1), .width(32), .disabled("Z"), .enable("false")) multiplexer_22 (
    .in0(in_25), .in1({32{1'b0}}), .out(multiplexer_22_out), .sel(in_3));
  Multiplexer #(.select(1), .width(16), .disabled("Z"), .enable("false")) multiplexer_23 (
    .in0(in_26), .in1({16{1'b0}}), .out(multiplexer_23_out), .sel(in_3));
  Pull_Resistor #(.pull(0)) pull_resistor_1 (.node(in_3));
  Pull_Resistor #(.pull(0)) pull_resistor_2 (.node(pull_resistor_2_node));
  not not_1 (pull_resistor_2_node, in_2);
  Register #(.width(1), .trigger("rising"), .Select("low")) register_1 (
    .D(multiplexer_1_out), .en(pull_resistor_2_node), .Q(out_29), .clk(in_1));  // open: clr
  Register #(.width(1), .trigger("rising"), .Select("low")) register_2 (
    .D(multiplexer_2_out), .en(pull_resistor_2_node), .Q(out_30), .clk(in_1));  // open: clr
  Register #(.width(1), .trigger("rising"), .Select("low")) register_3 (
    .D(multiplexer_3_out), .en(pull_resistor_2_node), .Q(out_31), .clk(in_1));  // open: clr
  Register #(.width(1), .trigger("rising"), .Select("low")) register_4 (
    .D(multiplexer_4_out), .en(pull_resistor_2_node), .Q(out_32), .clk(in_1));  // open: clr
  Register #(.width(4), .trigger("rising"), .Select("low")) register_5 (
    .D(multiplexer_5_out), .en(pull_resistor_2_node), .Q(out_33), .clk(in_1));  // open: clr
  Register #(.width(1), .trigger("rising"), .Select("low")) register_6 (
    .D(multiplexer_6_out), .en(pull_resistor_2_node), .Q(out_34), .clk(in_1));  // open: clr
  Register #(.width(1), .trigger("rising"), .Select("low")) register_7 (
    .D(multiplexer_7_out), .en(pull_resistor_2_node), .Q(out_35), .clk(in_1));  // open: clr
  Register #(.width(1), .trigger("rising"), .Select("low")) register_8 (
    .D(multiplexer_8_out), .en(pull_resistor_2_node), .Q(out_36), .clk(in_1));  // open: clr
  Register #(.width(1), .trigger("rising"), .Select("low")) register_9 (
    .D(multiplexer_9_out), .en(pull_resistor_2_node), .Q(out_37), .clk(in_1));  // open: clr
  Register #(.width(1), .trigger("rising"), .Select("low")) register_10 (
    .D(multiplexer_10_out), .en(pull_resistor_2_node), .Q(out_38), .clk(in_1));  // open: clr
  Register #(.width(1), .trigger("rising"), .Select("low")) register_11 (
    .D(multiplexer_11_out), .en(pull_resistor_2_node), .Q(out_39), .clk(in_1));  // open: clr
  Register #(.width(1), .trigger("rising"), .Select("low")) register_12 (
    .D(multiplexer_12_out), .en(pull_resistor_2_node), .Q(out_40), .clk(in_1));  // open: clr
  Register #(.width(1), .trigger("rising"), .Select("low")) register_13 (
    .D(multiplexer_13_out), .en(pull_resistor_2_node), .Q(out_41), .clk(in_1));  // open: clr
  Register #(.width(1), .trigger("rising"), .Select("low")) register_14 (
    .D(multiplexer_14_out), .en(pull_resistor_2_node), .Q(out_43), .clk(in_1));  // open: clr
  Register #(.width(1), .trigger("rising"), .Select("low")) register_15 (
    .D(multiplexer_15_out), .en(pull_resistor_2_node), .Q(out_44), .clk(in_1));  // open: clr
  Register #(.width(2), .trigger("rising"), .Select("low")) register_16 (
    .D(multiplexer_16_out), .en(pull_resistor_2_node), .Q(out_45), .clk(in_1));  // open: clr
  Register #(.width(2), .trigger("rising"), .Select("low")) register_17 (
    .D(multiplexer_17_out), .en(pull_resistor_2_node), .Q(out_46), .clk(in_1));  // open: clr
  Register #(.width(1), .trigger("rising"), .Select("low")) register_18 (
    .D(multiplexer_18_out), .en(pull_resistor_2_node), .Q(out_42), .clk(in_1));  // open: clr
  Register #(.width(32), .trigger("rising"), .Select("low")) register_19 (
    .D(multiplexer_19_out), .en(pull_resistor_2_node), .Q(out_27), .clk(in_1));  // open: clr
  Register #(.width(32), .trigger("rising"), .Select("low")) register_20 (
    .D(multiplexer_20_out), .en(pull_resistor_2_node), .Q(out_28), .clk(in_1));  // open: clr
  Register #(.width(32), .trigger("rising"), .Select("low")) register_21 (
    .D(multiplexer_21_out), .en(pull_resistor_2_node), .Q(out_47), .clk(in_1));  // open: clr
  Register #(.width(32), .trigger("rising"), .Select("low")) register_22 (
    .D(multiplexer_22_out), .en(pull_resistor_2_node), .Q(out_48), .clk(in_1));  // open: clr
  Register #(.width(16), .trigger("rising"), .Select("low")) register_23 (
    .D(multiplexer_23_out), .en(pull_resistor_2_node), .Q(out_49), .clk(in_1));  // open: clr

  // Other names for the same wires on the sheet: AIn[31:0] = in_24; AluOP[3:0] = in_10; AluOPOut[3:0] = out_33;
  //   AluSrcB = in_11; AluSrcBOut = out_34; AOut[31:0] = out_47; ASel[1:0] = in_22; ASelOut[1:0] = out_45; Beq = in_6;
  //   BeqOut = out_29; BIn[31:0] = in_25; BLTZ = in_17; BLTZOut = out_40; Bne = in_7; BneOut = out_30;
  //   BOut[31:0] = out_48; BSel[1:0] = in_23; BSelOut[1:0] = out_46; Clear = in_3; Clk = in_1; Enable = in_2;
  //   ImmIn[15:0] = in_26; ImmOut[15:0] = out_49; IRIn[31:0] = in_4; IROut[31:0] = out_27; JAL = in_14;
  //   JALOut = out_37; JMP = in_20; JMPOut = out_43; JR = in_21; JROut = out_44; MemToReg = in_9;
  //   MemToRegOut = out_32; MemWrite = in_8; MemWriteOut = out_31; PCIn[31:0] = in_5; PCOut[31:0] = out_28;
  //   RegDst = in_15; RegDstOut = out_38; RegWrite = in_13; RegWriteOut = out_36; RS_SHAMT = in_18;
  //   RS_SHAMTOut = out_41; SB = in_19; SBOut = out_42; SignedExt = in_12; SignedExtOut = out_35; Syscall = in_16;
  //   SyscallOut = out_39
endmodule

module EX_MEM (
  input  in_1,
  input  in_2,
  input  in_3,
  input  [31:0] in_4,
  input  [31:0] in_5,
  input  in_6,
  input  in_7,
  input  [31:0] in_8,
  input  [31:0] in_9,
  input  [31:0] in_10,
  input  in_11,
  input  in_12,
  input  in_13,
  input  in_14,
  input  in_15,
  output [31:0] out_16,
  output [31:0] out_17,
  output out_18,
  output out_19,
  output [31:0] out_20,
  output [31:0] out_21,
  output [31:0] out_22,
  output out_23,
  output out_24,
  output out_25,
  output out_26,
  output out_27
);

  wire multiplexer_1_out, multiplexer_2_out, multiplexer_3_out, multiplexer_4_out, multiplexer_5_out,
       multiplexer_6_out, multiplexer_7_out, pull_resistor_2_node;
  wire [31:0] multiplexer_8_out, multiplexer_9_out, multiplexer_10_out, multiplexer_11_out,
       multiplexer_12_out;

  Pull_Resistor #(.pull(0)) pull_resistor_1 (.node(in_3));
  Multiplexer #(.select(1), .width(1), .disabled("Z"), .enable("false")) multiplexer_1 (
    .in0(in_6), .in1(1'b0), .out(multiplexer_1_out), .sel(in_3));
  Multiplexer #(.select(1), .width(1), .disabled("Z"), .enable("false")) multiplexer_2 (
    .in0(in_7), .in1(1'b0), .out(multiplexer_2_out), .sel(in_3));
  Multiplexer #(.select(1), .width(1), .disabled("Z"), .enable("false")) multiplexer_3 (
    .in0(in_11), .in1(1'b0), .out(multiplexer_3_out), .sel(in_3));
  Multiplexer #(.select(1), .width(1), .disabled("Z"), .enable("false")) multiplexer_4 (
    .in0(in_12), .in1(1'b0), .out(multiplexer_4_out), .sel(in_3));
  Multiplexer #(.select(1), .width(1), .disabled("Z"), .enable("false")) multiplexer_5 (
    .in0(in_13), .in1(1'b0), .out(multiplexer_5_out), .sel(in_3));
  Multiplexer #(.select(1), .width(1), .disabled("Z"), .enable("false")) multiplexer_6 (
    .in0(in_14), .in1(1'b0), .out(multiplexer_6_out), .sel(in_3));
  Multiplexer #(.select(1), .width(1), .disabled("Z"), .enable("false")) multiplexer_7 (
    .in0(in_15), .in1(1'b0), .out(multiplexer_7_out), .sel(in_3));
  Multiplexer #(.select(1), .width(32), .disabled("Z"), .enable("false")) multiplexer_8 (
    .in0(in_4), .in1({32{1'b0}}), .out(multiplexer_8_out), .sel(in_3));
  Multiplexer #(.select(1), .width(32), .disabled("Z"), .enable("false")) multiplexer_9 (
    .in0(in_5), .in1({32{1'b0}}), .out(multiplexer_9_out), .sel(in_3));
  Multiplexer #(.select(1), .width(32), .disabled("Z"), .enable("false")) multiplexer_10 (
    .in0(in_8), .in1({32{1'b0}}), .out(multiplexer_10_out), .sel(in_3));
  Multiplexer #(.select(1), .width(32), .disabled("Z"), .enable("false")) multiplexer_11 (
    .in0(in_9), .in1({32{1'b0}}), .out(multiplexer_11_out), .sel(in_3));
  Multiplexer #(.select(1), .width(32), .disabled("Z"), .enable("false")) multiplexer_12 (
    .in0(in_10), .in1({32{1'b0}}), .out(multiplexer_12_out), .sel(in_3));
  Pull_Resistor #(.pull(0)) pull_resistor_2 (.node(pull_resistor_2_node));
  not not_1 (pull_resistor_2_node, in_2);
  Register #(.width(1), .trigger("rising"), .Select("low")) register_1 (
    .D(multiplexer_1_out), .en(pull_resistor_2_node), .Q(out_18), .clk(in_1));  // open: clr
  Register #(.width(1), .trigger("rising"), .Select("low")) register_2 (
    .D(multiplexer_2_out), .en(pull_resistor_2_node), .Q(out_19), .clk(in_1));  // open: clr
  Register #(.width(1), .trigger("rising"), .Select("low")) register_3 (
    .D(multiplexer_3_out), .en(pull_resistor_2_node), .Q(out_23), .clk(in_1));  // open: clr
  Register #(.width(1), .trigger("rising"), .Select("low")) register_4 (
    .D(multiplexer_4_out), .en(pull_resistor_2_node), .Q(out_24), .clk(in_1));  // open: clr
  Register #(.width(1), .trigger("rising"), .Select("low")) register_5 (
    .D(multiplexer_5_out), .en(pull_resistor_2_node), .Q(out_25), .clk(in_1));  // open: clr
  Register #(.width(1), .trigger("rising"), .Select("low")) register_6 (
    .D(multiplexer_6_out), .en(pull_resistor_2_node), .Q(out_26), .clk(in_1));  // open: clr
  Register #(.width(1), .trigger("rising"), .Select("low")) register_7 (
    .D(multiplexer_7_out), .en(pull_resistor_2_node), .Q(out_27), .clk(in_1));  // open: clr
  Register #(.width(32), .trigger("rising"), .Select("low")) register_8 (
    .D(multiplexer_8_out), .en(pull_resistor_2_node), .Q(out_16), .clk(in_1));  // open: clr
  Register #(.width(32), .trigger("rising"), .Select("low")) register_9 (
    .D(multiplexer_9_out), .en(pull_resistor_2_node), .Q(out_17), .clk(in_1));  // open: clr
  Register #(.width(32), .trigger("rising"), .Select("low")) register_10 (
    .D(multiplexer_10_out), .en(pull_resistor_2_node), .Q(out_20), .clk(in_1));  // open: clr
  Register #(.width(32), .trigger("rising"), .Select("low")) register_11 (
    .D(multiplexer_11_out), .en(pull_resistor_2_node), .Q(out_21), .clk(in_1));  // open: clr
  Register #(.width(32), .trigger("rising"), .Select("low")) register_12 (
    .D(multiplexer_12_out), .en(pull_resistor_2_node), .Q(out_22), .clk(in_1));  // open: clr

  // Other names for the same wires on the sheet: AIn[31:0] = in_8; ALUIn[31:0] = in_10; ALUOut[31:0] = out_22;
  //   AOut[31:0] = out_20; BIn[31:0] = in_9; BOut[31:0] = out_21; Clear = in_3; Clk = in_1; Enable = in_2;
  //   IRIn[31:0] = in_4; IROut[31:0] = out_16; JAL = in_12; JALOut = out_24; MemToReg = in_7; MemToRegOut = out_19;
  //   MemWrite = in_6; MemWriteOut = out_18; PCIn[31:0] = in_5; PCOut[31:0] = out_17; RegDst = in_13;
  //   RegDstOut = out_25; RegWrite = in_11; RegWriteOut = out_23; SB = in_15; SBOut = out_27; Syscall = in_14;
  //   SyscallOut = out_26
endmodule

module MEM_WB (
  input  in_1,
  input  in_2,
  input  in_3,
  input  [31:0] in_4,
  input  [31:0] in_5,
  input  in_6,
  input  [31:0] in_7,
  input  [31:0] in_8,
  input  [31:0] in_9,
  input  [31:0] in_10,
  input  in_11,
  input  in_12,
  input  in_13,
  input  in_14,
  output [31:0] out_15,
  output [31:0] out_16,
  output out_17,
  output [31:0] out_18,
  output [31:0] out_19,
  output [31:0] out_20,
  output [31:0] out_21,
  output out_22,
  output out_23,
  output out_24,
  output out_25
);

  wire multiplexer_5_out, multiplexer_6_out, multiplexer_7_out, multiplexer_8_out, multiplexer_9_out,
       pull_resistor_2_node;
  wire [31:0] multiplexer_1_out, multiplexer_2_out, multiplexer_3_out, multiplexer_4_out, multiplexer_10_out,
       multiplexer_11_out;

  Pull_Resistor #(.pull(0)) pull_resistor_1 (.node(in_3));
  Multiplexer #(.select(1), .width(32), .disabled("Z"), .enable("false")) multiplexer_1 (
    .in0(in_4), .in1({32{1'b0}}), .out(multiplexer_1_out), .sel(in_3));
  Multiplexer #(.select(1), .width(32), .disabled("Z"), .enable("false")) multiplexer_2 (
    .in0(in_7), .in1({32{1'b0}}), .out(multiplexer_2_out), .sel(in_3));
  Multiplexer #(.select(1), .width(32), .disabled("Z"), .enable("false")) multiplexer_3 (
    .in0(in_8), .in1({32{1'b0}}), .out(multiplexer_3_out), .sel(in_3));
  Multiplexer #(.select(1), .width(32), .disabled("Z"), .enable("false")) multiplexer_4 (
    .in0(in_5), .in1({32{1'b0}}), .out(multiplexer_4_out), .sel(in_3));
  Multiplexer #(.select(1), .width(1), .disabled("Z"), .enable("false")) multiplexer_5 (
    .in0(in_6), .in1(1'b0), .out(multiplexer_5_out), .sel(in_3));
  Multiplexer #(.select(1), .width(1), .disabled("Z"), .enable("false")) multiplexer_6 (
    .in0(in_12), .in1(1'b0), .out(multiplexer_6_out), .sel(in_3));
  Multiplexer #(.select(1), .width(1), .disabled("Z"), .enable("false")) multiplexer_7 (
    .in0(in_11), .in1(1'b0), .out(multiplexer_7_out), .sel(in_3));
  Multiplexer #(.select(1), .width(1), .disabled("Z"), .enable("false")) multiplexer_8 (
    .in0(in_13), .in1(1'b0), .out(multiplexer_8_out), .sel(in_3));
  Multiplexer #(.select(1), .width(1), .disabled("Z"), .enable("false")) multiplexer_9 (
    .in0(in_14), .in1(1'b0), .out(multiplexer_9_out), .sel(in_3));
  Multiplexer #(.select(1), .width(32), .disabled("Z"), .enable("false")) multiplexer_10 (
    .in0(in_10), .in1({32{1'b0}}), .out(multiplexer_10_out), .sel(in_3));
  Multiplexer #(.select(1), .width(32), .disabled("Z"), .enable("false")) multiplexer_11 (
    .in0(in_9), .in1({32{1'b0}}), .out(multiplexer_11_out), .sel(in_3));
  Pull_Resistor #(.pull(0)) pull_resistor_2 (.node(pull_resistor_2_node));
  not not_1 (pull_resistor_2_node, in_2);
  Register #(.width(32), .trigger("rising"), .Select("low")) register_1 (
    .D(multiplexer_1_out), .en(pull_resistor_2_node), .Q(out_15), .clk(in_1));  // open: clr
  Register #(.width(32), .trigger("rising"), .Select("low")) register_2 (
    .D(multiplexer_2_out), .en(pull_resistor_2_node), .Q(out_18), .clk(in_1));  // open: clr
  Register #(.width(32), .trigger("rising"), .Select("low")) register_3 (
    .D(multiplexer_3_out), .en(pull_resistor_2_node), .Q(out_19), .clk(in_1));  // open: clr
  Register #(.width(32), .trigger("rising"), .Select("low")) register_4 (
    .D(multiplexer_4_out), .en(pull_resistor_2_node), .Q(out_16), .clk(in_1));  // open: clr
  Register #(.width(1), .trigger("rising"), .Select("low")) register_5 (
    .D(multiplexer_5_out), .en(pull_resistor_2_node), .Q(out_17), .clk(in_1));  // open: clr
  Register #(.width(1), .trigger("rising"), .Select("low")) register_6 (
    .D(multiplexer_6_out), .en(pull_resistor_2_node), .Q(out_23), .clk(in_1));  // open: clr
  Register #(.width(1), .trigger("rising"), .Select("low")) register_7 (
    .D(multiplexer_7_out), .en(pull_resistor_2_node), .Q(out_22), .clk(in_1));  // open: clr
  Register #(.width(1), .trigger("rising"), .Select("low")) register_8 (
    .D(multiplexer_8_out), .en(pull_resistor_2_node), .Q(out_24), .clk(in_1));  // open: clr
  Register #(.width(1), .trigger("rising"), .Select("low")) register_9 (
    .D(multiplexer_9_out), .en(pull_resistor_2_node), .Q(out_25), .clk(in_1));  // open: clr
  Register #(.width(32), .trigger("rising"), .Select("low")) register_10 (
    .D(multiplexer_10_out), .en(pull_resistor_2_node), .Q(out_21), .clk(in_1));  // open: clr
  Register #(.width(32), .trigger("rising"), .Select("low")) register_11 (
    .D(multiplexer_11_out), .en(pull_resistor_2_node), .Q(out_20), .clk(in_1));  // open: clr

  // Other names for the same wires on the sheet: A[31:0] = in_7; ALUIn[31:0] = in_10; ALUOut[31:0] = out_21;
  //   AOut[31:0] = out_18; B[31:0] = in_8; BOut[31:0] = out_19; Clear = in_3; Clk = in_1; Enable = in_2;
  //   IRIn[31:0] = in_4; IROut[31:0] = out_15; JAL = in_12; JALOut = out_23; MDIn[31:0] = in_9; MDOut[31:0] = out_20;
  //   MemToReg = in_6; MemToRegOut = out_17; PCin[31:0] = in_5; PCout[31:0] = out_16; RegDst = in_13;
  //   RegDstOut = out_24; RegWrite = in_11; RegWriteOut = out_22; Syscall = in_14; SyscallOut = out_25
endmodule

module \数据相关检测  (
  input  [4:0] in_1,
  input  [4:0] in_2,
  input  [4:0] in_3,
  input  [4:0] in_4,
  input  in_5,
  input  in_6,
  input  in_7,
  input  in_8,
  input  in_9,
  output out_10
);

  wire and_1_out, and_2_out, and_3_out, and_4_out, comparator_1_eq, comparator_2_eq, comparator_3_eq,
       comparator_4_eq, comparator_5_eq, comparator_6_eq, or_1_out;

  Comparator #(.width(5), .mode("twosComplement")) comparator_1 (
    .a(in_1), .b({5{1'b0}}), .eq(comparator_1_eq));  // open: gt, lt
  Comparator #(.width(5), .mode("twosComplement")) comparator_2 (
    .a(in_1), .b(in_3), .eq(comparator_2_eq));  // open: gt, lt
  Comparator #(.width(5), .mode("twosComplement")) comparator_3 (
    .a(in_2), .b({5{1'b0}}), .eq(comparator_3_eq));  // open: gt, lt
  Comparator #(.width(5), .mode("twosComplement")) comparator_4 (
    .a(in_2), .b(in_3), .eq(comparator_4_eq));  // open: gt, lt
  Comparator #(.width(5), .mode("twosComplement")) comparator_5 (
    .a(in_1), .b(in_4), .eq(comparator_5_eq));  // open: gt, lt
  Comparator #(.width(5), .mode("twosComplement")) comparator_6 (
    .a(in_2), .b(in_4), .eq(comparator_6_eq));  // open: gt, lt
  and and_1 (and_1_out, ~comparator_1_eq, comparator_2_eq, in_7, in_5);  // AND_Gate
  and and_2 (and_2_out, ~comparator_3_eq, comparator_4_eq, in_8, in_5);  // AND_Gate
  and and_3 (and_3_out, ~comparator_1_eq, comparator_5_eq, in_7, in_6);  // AND_Gate
  and and_4 (and_4_out, ~comparator_3_eq, comparator_6_eq, in_8, in_6);  // AND_Gate
  or or_1 (or_1_out, and_1_out, and_2_out, and_3_out, and_4_out);
  and and_5 (out_10, or_1_out, in_9);

  // Other names for the same wires on the sheet: dataCheck = out_10; EXRegWrite = in_5; EXWriteReg[4:0] = in_3;
  //   MEMRegWrite = in_6; MEMWriteReg[4:0] = in_4; R1_Used = in_7; R2_Used = in_8; RegA[4:0] = in_1; RegB[4:0] = in_2;
  //   Running = in_9
endmodule

module \重定向数据相关检测  (
  input  [4:0] in_1,
  input  [4:0] in_2,
  input  [4:0] in_3,
  input  [4:0] in_4,
  input  in_5,
  input  in_6,
  input  in_7,
  input  in_8,
  input  in_9,
  input  in_10,
  input  in_11,
  output [1:0] out_12,
  output [1:0] out_13,
  output out_14
);

  wire A_EX_out, A_MEM_out, and_1_out, and_2_out, and_3_out, and_4_out, B_EX_out, B_MEM_out, comparator_1_eq,
       comparator_2_eq, comparator_3_eq, comparator_4_eq, comparator_5_eq, comparator_6_eq, or_1_out;
  wire [1:0] multiplexer_1_out, multiplexer_2_out;

  Comparator #(.width(5), .mode("twosComplement")) comparator_1 (
    .a(in_1), .b({5{1'b0}}), .eq(comparator_1_eq));  // open: gt, lt
  Comparator #(.width(5), .mode("twosComplement")) comparator_2 (
    .a(in_1), .b(in_3), .eq(comparator_2_eq));  // open: gt, lt
  Comparator #(.width(5), .mode("twosComplement")) comparator_3 (
    .a(in_2), .b({5{1'b0}}), .eq(comparator_3_eq));  // open: gt, lt
  Comparator #(.width(5), .mode("twosComplement")) comparator_4 (
    .a(in_2), .b(in_3), .eq(comparator_4_eq));  // open: gt, lt
  Comparator #(.width(5), .mode("twosComplement")) comparator_5 (
    .a(in_1), .b(in_4), .eq(comparator_5_eq));  // open: gt, lt
  Comparator #(.width(5), .mode("twosComplement")) comparator_6 (
    .a(in_2), .b(in_4), .eq(comparator_6_eq));  // open: gt, lt
  and A_EX (A_EX_out, ~comparator_1_eq, comparator_2_eq, in_8, in_5);  // AND_Gate
  and B_EX (B_EX_out, ~comparator_3_eq, comparator_4_eq, in_9, in_5);  // AND_Gate
  and A_MEM (A_MEM_out, ~comparator_1_eq, comparator_5_eq, in_8, in_6);  // AND_Gate
  and B_MEM (B_MEM_out, ~comparator_3_eq, comparator_6_eq, in_9, in_6);  // AND_Gate
  and and_1 (and_1_out, A_EX_out, ~in_7);  // AND_Gate
  and and_2 (and_2_out, A_EX_out, in_7);
  and and_3 (and_3_out, B_EX_out, ~in_7);  // AND_Gate
  and and_4 (and_4_out, B_EX_out, in_7);
  Multiplexer #(.select(1), .width(2), .disabled("Z"), .enable("false")) multiplexer_1 (
    .in0(2'b00), .in1({1'b1, in_11}), .out(multiplexer_1_out), .sel(A_MEM_out));
  Multiplexer #(.select(1), .width(2), .disabled("Z"), .enable("false")) multiplexer_2 (
    .in0(2'b00), .in1({1'b1, in_11}), .out(multiplexer_2_out), .sel(B_MEM_out));
  Multiplexer #(.select(1), .width(2), .disabled("Z"), .enable("false")) multiplexer_3 (
    .in0(multiplexer_1_out), .in1(2'b01), .out(out_12), .sel(and_1_out));
  Multiplexer #(.select(1), .width(2), .disabled("Z"), .enable("false")) multiplexer_4 (
    .in0(multiplexer_2_out), .in1(2'b01), .out(out_13), .sel(and_3_out));
  or or_1 (or_1_out, and_2_out, and_4_out);
  and and_5 (out_14, or_1_out, in_10);

  // Other names for the same wires on the sheet: MEMMemToReg = in_11; EXMemToReg = in_7; EXRegWrite = in_5;
  //   EXWriteReg[4:0] = in_3; Forward1[1:0] = out_12; Forward2[1:0] = out_13; LoadUse = out_14; MEMRegWrite = in_6;
  //   MEMWriteReg[4:0] = in_4; R1_Used = in_8; R2_Used = in_9; RegA[4:0] = in_1; RegB[4:0] = in_2; Running = in_10
endmodule
